# Fritzing sketch IO_board (saved by Fritzing 0.9.0b)
circuit board: 7.6cm x 10.9cm
breadboards: 1

parts:
  LEDR = LED - 5mm [color="Red (633nm)" package="5 mm [THT]"]
  DIP = IC, DIP package, 8 pins [chip_label=DIP]
  J15 = male pin header, 1 pin [form="♂ (male)"]
  J16 = male pin header, 1 pin [form="♂ (male)"]
  MCP23017 = IC, DIP package, 28 pins [chip_label=IC]
  MCP23017_2 = IC, DIP package, 28 pins [chip_label=IC]
  ULN2803A = IC, DIP package, 18 pins [chip_label=IC]
  ULN2803A_2 = IC, DIP package, 18 pins [chip_label=IC]
  UART8 = male pin header, 8 pins [form="♂ (male)"]
  UART9 = male pin header, 8 pins [form="♂ (male)"]
  UART10 = male pin header, 8 pins [form="♂ (male)"]
  UART11 = male pin header, 8 pins [form="♂ (male)"]
  UART12 = male pin header, 4 pins [form="♂ (male)"]
  UART13 = male pin header, 4 pins [form="♂ (male)"]
  UART14 = male pin header, 4 pins [form="♂ (male)"]
  UART15 = male pin header, 6 pins [form="♂ (male)"]
  UART17 = male pin header, 10 pins [form="♂ (male)"]
  UART26 = male pin header, 5 pins [form="♂ (male)"]
  UART27 = male pin header, 5 pins [form="♂ (male)"]
  J25 = double row male pin header, 20 pins [form="♂ (male)"]
  UART28 = male pin header, 4 pins [form="♂ (male)"]
  UART16 = male pin header, 6 pins [form="♂ (male)"]
  LEDG = LED - 5mm [color="Green (570nm)" package="5 mm [THT]"]
  UART19 = male pin header, 9 pins [form="♂ (male)"]
  MCP23017_3 = IC, DIP package, 28 pins [chip_label=IC]
  UART36 = male pin header, 8 pins [form="♂ (male)"]
  J27 = male pin header, 8 pins [form="♂ (male)"]
  UART29 = male pin header, 24 pins [form="♂ (male)"]
  UART37 = double row male pin header, 14 pins [form="♂ (male)"]
  UART38 = double row male pin header, 14 pins [form="♂ (male)"]
  S4 = Momentary Switch [package=ksa_sealed_tac_switch]
  S3 = Momentary Switch [package=ksa_sealed_tac_switch]
  S2 = Momentary Switch [package=ksa_sealed_tac_switch]
  S1 = Momentary Switch [package=ksa_sealed_tac_switch]
  J34 = screw terminal, 2 pins
  UART39 = male pin header, 8 pins [form="♂ (male)"]
  UART40 = male pin header, 4 pins [form="♂ (male)"]
  UART41 = male pin header, 4 pins [form="♂ (male)"]

nets:
  N1: LEDR.cathode, DIP.pin5, DIP.pin6, DIP.pin7, DIP.pin8, J15.pin1, MCP23017.pin10, MCP23017.pin16, MCP23017.pin17, MCP23017_2.pin10, MCP23017_2.pin15, MCP23017_2.pin16, MCP23017_2.pin17, ULN2803A.pin9, ULN2803A_2.pin9, UART15.pin5, UART17.pin1, UART27.pin5, UART16.pin2, UART16.pin5, LEDG.cathode, MCP23017_3.pin10, MCP23017_3.pin15, MCP23017_3.pin17, S4.1, S3.1, S2.1, S1.1, J34.pin1, J34.pin2
  N2: LEDR.anode, MCP23017_2.pin26
  N3: DIP.pin1, MCP23017_2.pin7
  N4: DIP.pin2, MCP23017_2.pin6
  N5: DIP.pin3, MCP23017_2.pin5
  N6: DIP.pin4, MCP23017_2.pin4
  N7: J16.pin1, MCP23017_2.pin27
  N8: MCP23017.pin1, UART11.pin8
  N9: MCP23017.pin2, UART11.pin7
  N10: MCP23017.pin3, UART11.pin6
  N11: MCP23017.pin4, UART11.pin5
  N12: MCP23017.pin5, UART11.pin4
  N13: MCP23017.pin6, UART11.pin3
  N14: MCP23017.pin7, UART11.pin2
  N15: MCP23017.pin8, UART11.pin1
  N16: MCP23017.pin9, MCP23017.pin15, MCP23017.pin18, MCP23017_2.pin9, MCP23017_2.pin18, UART15.pin2, UART15.pin6, UART17.pin10, UART26.pin5, UART16.pin6, MCP23017_3.pin9, MCP23017_3.pin16, MCP23017_3.pin18, UART37.pin8
  N17: MCP23017.pin12, MCP23017_2.pin12, UART15.pin4, UART26.pin4, J25.pin1, J25.pin2, J25.pin3, J25.pin4, J25.pin5, J25.pin6, J25.pin7, J25.pin8, J25.pin9, J25.pin10, UART16.pin4, MCP23017_3.pin12, UART38.pin14
  N18: MCP23017.pin13, MCP23017_2.pin13, UART26.pin3, J25.pin11, J25.pin12, J25.pin13, J25.pin14, J25.pin15, J25.pin16, J25.pin17, J25.pin18, J25.pin19, J25.pin20, UART16.pin3, MCP23017_3.pin13, UART38.pin13
  N19: MCP23017.pin21, UART10.pin1
  N20: MCP23017.pin22, UART10.pin2
  N21: MCP23017.pin23, UART10.pin3
  N22: MCP23017.pin24, UART10.pin4
  N23: MCP23017.pin25, UART10.pin5
  N24: MCP23017.pin26, UART10.pin6
  N25: MCP23017.pin27, UART10.pin7
  N26: MCP23017.pin28, UART10.pin8
  N27: MCP23017_2.pin1, S2.4
  N28: MCP23017_2.pin2, S1.4
  N29: MCP23017_2.pin3, S3.4
  N30: MCP23017_2.pin21, UART12.pin1
  N31: MCP23017_2.pin22, UART12.pin2
  N32: MCP23017_2.pin23, UART12.pin3
  N33: MCP23017_2.pin24, UART12.pin4
  N34: MCP23017_2.pin25, LEDG.anode
  N35: MCP23017_2.pin28, S4.4
  N36: ULN2803A.pin1, MCP23017_3.pin28
  N37: ULN2803A.pin2, MCP23017_3.pin27
  N38: ULN2803A.pin3, MCP23017_3.pin26
  N39: ULN2803A.pin4, MCP23017_3.pin25
  N40: ULN2803A.pin5, MCP23017_3.pin24
  N41: ULN2803A.pin6, MCP23017_3.pin23
  N42: ULN2803A.pin7, MCP23017_3.pin22
  N43: ULN2803A.pin8, MCP23017_3.pin21
  N44: ULN2803A.pin11, UART8.pin1
  N45: ULN2803A.pin12, UART8.pin2
  N46: ULN2803A.pin13, UART8.pin3
  N47: ULN2803A.pin14, UART8.pin4
  N48: ULN2803A.pin15, UART8.pin5
  N49: ULN2803A.pin16, UART8.pin6
  N50: ULN2803A.pin17, UART8.pin7
  N51: ULN2803A.pin18, UART8.pin8
  N52: ULN2803A_2.pin1, MCP23017_3.pin8
  N53: ULN2803A_2.pin2, MCP23017_3.pin7
  N54: ULN2803A_2.pin3, MCP23017_3.pin6
  N55: ULN2803A_2.pin4, MCP23017_3.pin5
  N56: ULN2803A_2.pin5, MCP23017_3.pin4
  N57: ULN2803A_2.pin6, MCP23017_3.pin3
  N58: ULN2803A_2.pin7, MCP23017_3.pin2
  N59: ULN2803A_2.pin8, MCP23017_3.pin1
  N60: ULN2803A_2.pin11, UART9.pin8
  N61: ULN2803A_2.pin12, UART9.pin7
  N62: ULN2803A_2.pin13, UART9.pin6
  N63: ULN2803A_2.pin14, UART9.pin5
  N64: ULN2803A_2.pin15, UART9.pin4
  N65: ULN2803A_2.pin16, UART9.pin3
  N66: ULN2803A_2.pin17, UART9.pin2
  N67: ULN2803A_2.pin18, UART9.pin1
  N68: UART13.pin1, UART40.pin1
  N69: UART13.pin2, UART40.pin2
  N70: UART13.pin3, UART40.pin3
  N71: UART13.pin4, UART40.pin4
  N72: UART14.pin1, UART41.pin4
  N73: UART14.pin2, UART41.pin3
  N74: UART14.pin3, UART41.pin2
  N75: UART14.pin4, UART41.pin1
  N76: UART17.pin2, UART39.pin1
  N77: UART17.pin3, UART39.pin2
  N78: UART17.pin4, UART39.pin3
  N79: UART17.pin5, UART39.pin4
  N80: UART17.pin6, UART39.pin5
  N81: UART17.pin7, UART39.pin6
  N82: UART17.pin8, UART39.pin7
  N83: UART17.pin9, UART39.pin8
  N84: UART27.pin1, UART28.pin4
  N85: UART27.pin2, UART28.pin3
  N86: UART27.pin3, UART28.pin2
  N87: UART27.pin4, UART28.pin1
  N88: UART19.pin1, J27.pin1
  N89: UART19.pin2, J27.pin2
  N90: UART19.pin3, J27.pin3
  N91: UART19.pin4, J27.pin4
  N92: UART19.pin5, J27.pin5
  N93: UART19.pin6, J27.pin6
  N94: UART19.pin7, J27.pin7
  N95: UART19.pin8, J27.pin8
  N96: UART19.pin9, UART37.pin9
  N97: UART36.pin1, UART29.pin1, UART37.pin7
  N98: UART36.pin2, UART29.pin2, UART37.pin10
  N99: UART36.pin3, UART29.pin3, UART37.pin11
  N100: UART36.pin4, UART29.pin4, UART37.pin12
  N101: UART36.pin5, UART29.pin5, UART37.pin13
  N102: UART36.pin6, UART29.pin6, UART37.pin14
  N103: UART36.pin7, UART29.pin7, UART37.pin1
  N104: UART36.pin8, UART29.pin8, UART37.pin2
  N105: UART29.pin9, UART37.pin3
  N106: UART29.pin10, UART37.pin4
  N107: UART29.pin11, UART37.pin5
  N108: UART29.pin12, UART37.pin6
  N109: UART29.pin13, UART38.pin4
  N110: UART29.pin14, UART38.pin5
  N111: UART29.pin15, UART38.pin6
  N112: UART29.pin16, UART38.pin7
  N113: UART29.pin17, UART38.pin8
  N114: UART29.pin18, UART38.pin9
  N115: UART29.pin19, UART38.pin10
  N116: UART29.pin20, UART38.pin11
  N117: UART29.pin21, UART38.pin12
  N118: UART29.pin22, UART38.pin3
  N119: UART29.pin23, UART38.pin2
  N120: UART29.pin24, UART38.pin1

notes:
  XGPIO21
  SUM
  GPIO04
  1
  DIPL1
  I2C
  SDA
  +5V
  GND
  SCL
  A2 A1 A0
  3
  6
  4
  7
  5
  2
  0
  8
  11
  12
  14
  16
  15
  10
  13
  9
  XGPIO20
  XGPIO22
  2 * ADS1015
  ADDR
  A0
  A1
  A2
  A3
  +3V3
  22
  21
  20
  17
  18
  19
  23
  24
  TXB0108
  Vo4
  Vo3
  Vo2
  Vo1
  MCP4728
  STEELSQUID.ORG
  SteelsquidPiCon
  SPCIB10
  IO Board V1.0
  PIGPIO3V3
  PIGPIO5V
  DAC60
  <-ADC48
  RELAY->
  ADC48
  <---ADC49
  PWM
  PIN----->
  GPIO---->
  09
  05
  27
  04
  26
  06
  07
  08
  25
  <-GPIO
  <--PIN
  PIN
