# Fritzing sketch gpio_board 4 (saved by Fritzing 0.9.0b)
circuit board: 5.4cm x 5.4cm
breadboards: 1

parts:
  J35 = double row male pin header, 14 pins [form="♂ (male)"]
  J36 = male pin header, 20 pins [form="♂ (male)"]
  J38 = male pin header, 20 pins [form="♂ (male)"]
  J39 = double row male pin header, 14 pins [form="♂ (male)"]
  J40 = screw terminal, 2 pins
  J41 = screw terminal, 2 pins
  J37 = male pin header, 6 pins [form="♂ (male)"]
  J42 = male pin header, 6 pins [form="♂ (male)"]
  J43 = male pin header, 4 pins [form="♂ (male)"]
  J44 = male pin header, 4 pins [form="♂ (male)"]

nets:
  N1: J35.pin1, J38.pin1
  N2: J35.pin2, J38.pin2
  N3: J35.pin3, J38.pin3
  N4: J35.pin4, J38.pin5
  N5: J35.pin5, J38.pin8
  N6: J35.pin6, J38.pin9
  N7: J35.pin7, J38.pin10
  N8: J35.pin8, J38.pin20, J40.pin2, J44.pin1, J44.pin2, J44.pin3, J44.pin4
  N9: J35.pin9, J36.pin20, J40.pin1, J43.pin1, J43.pin2, J43.pin3, J43.pin4
  N10: J35.pin10, J38.pin12
  N11: J35.pin11, J38.pin13
  N12: J35.pin12, J38.pin15
  N13: J35.pin13, J38.pin16
  N14: J35.pin14, J38.pin17
  N15: J36.pin2, J39.pin7
  N16: J36.pin3, J39.pin6
  N17: J36.pin4, J39.pin5
  N18: J36.pin5, J39.pin4
  N19: J36.pin6, J39.pin3
  N20: J36.pin9, J39.pin2
  N21: J36.pin10, J39.pin1
  N22: J36.pin11, J39.pin12
  N23: J36.pin13, J39.pin11
  N24: J36.pin14, J39.pin10
  N25: J36.pin15, J39.pin9
  N26: J36.pin17, J39.pin8
  N27: J36.pin18, J39.pin14, J37.pin2, J37.pin4, J37.pin6, J42.pin2, J42.pin4, J42.pin6
  N28: J36.pin19, J39.pin13, J37.pin1, J37.pin3, J37.pin5, J42.pin1, J42.pin3, J42.pin5
  N29: J38.pin18, J41.pin1, J41.pin2

notes:
  24
  SDL
  SDA
  I2C
  SteelsquidPiCon
  STEELSQUID.ORG
  GPIO Board V1.0
  SPCGB10
  GND(trex)
  GND(iob)
  +5V_in
  +3V3_out
  10
  04
  17
  27
  22
  09
  11
  05
  06
  13
  19
  26
  14
  15
  18
  23
  +3V3
  +5V
  21
  20
  16
  12
  07
  08
  25
