# Fritzing sketch main_board (saved by Fritzing 0.9.0b)
circuit board: 16cm x 10cm
breadboards: 1

parts:
  J7 = male pin header, 7 pins [form="♂ (male)"]
  J8 = male pin header, 7 pins [form="♂ (male)"]
  J15 = male pin header, 6 pins [form="♂ (male)"]
  J16 = male pin header, 4 pins [form="♂ (male)"]
  J18 = male pin header, 1 pin [form="♂ (male)"]
  J17 = male pin header, 1 pin [form="♂ (male)"]
  J25 = double row male pin header, 8 pins [form="♂ (male)"]
  J26 = male pin header, 8 pins [form="♂ (male)"]
  UART27 = male pin header, 6 pins [form="♂ (male)"]
  UART28 = male pin header, 6 pins [form="♂ (male)"]
  UART29 = male pin header, 6 pins [form="♂ (male)"]
  UART30 = male pin header, 6 pins [form="♂ (male)"]

nets:
  N1: J7.pin1, J7.pin2, J7.pin3, J7.pin4, J7.pin5, J7.pin6, J7.pin7
  N2: J8.pin1, J8.pin2, J8.pin3, J8.pin4, J8.pin5, J8.pin6, J8.pin7, J15.pin5, J17.pin1, UART29.pin1, UART29.pin2, UART29.pin3, UART29.pin4, UART29.pin5, UART29.pin6
  N3: J15.pin1, J16.pin4
  N4: J15.pin2, J16.pin3
  N5: J15.pin3, J16.pin2
  N6: J15.pin4, J16.pin1
  N7: J15.pin6, J18.pin1
  N8: J25.pin1, J26.pin8
  N9: J25.pin2, J26.pin6
  N10: J25.pin3, J26.pin4
  N11: J25.pin4, J26.pin2
  N12: J25.pin5, J26.pin1
  N13: J25.pin6, J26.pin3
  N14: J25.pin7, J26.pin5
  N15: J25.pin8, J26.pin7
  N16: UART27.pin1, UART30.pin6
  N17: UART27.pin2, UART30.pin5
  N18: UART27.pin3, UART30.pin4
  N19: UART27.pin4, UART30.pin3
  N20: UART27.pin5, UART30.pin2
  N21: UART27.pin6, UART30.pin1
  N22: UART28.pin1, UART28.pin2, UART28.pin3, UART28.pin4, UART28.pin5, UART28.pin6

notes:
  +V_out
  GND
  POWERB
  TREX
  +V_in
  +5V_out
  STEELSQUID.ORG
  SteelsquidPiCon
  Main Board V1.0 (SPCMB10)
  USB to TTL card
  1
  LCD1602
  9
  MVOT
  +5V
  2
  3
  4
  To Power Board
  -
  Screw Terminal
  RELAY
  SCREWIN
  SCREWOUT
  PINOUT
  4 Port Relay Card
  USB hub
  Raspberry Pi Model B+
  Voltage Reg
  LCD Board
  TXD
  RXD
  UART
  TXD 1
  RXD 1
  RXD 2
  TXD 2
  RXD 3
  TXD 3
  RXD 4
  TXD 4
  6
  5
  SERVO
  +6V
  PWM
