# Fritzing sketch power_board (saved by Fritzing 0.9.0b)
circuit board: 11.5cm x 4cm
breadboards: 1

parts:
  J13 = screw terminal, 2 pins
  J15 = double row male pin header, 24 pins [form="♂ (male)"]
  J16 = screw terminal, 2 pins
  J17 = double row male pin header, 24 pins [form="♂ (male)"]
  J18 = screw terminal, 2 pins
  J19 = double row male pin header, 24 pins [form="♂ (male)"]
  J20 = screw terminal, 2 pins
  J21 = double row male pin header, 24 pins [form="♂ (male)"]
  J22 = screw terminal, 2 pins
  J23 = double row male pin header, 24 pins [form="♂ (male)"]
  J24 = male pin header, 1 pin [form="♂ (male)"]  # not connected

nets:
  N1: J13.pin1, J13.pin2, J15.pin1, J15.pin2, J15.pin3, J15.pin4, J15.pin5, J15.pin6, J15.pin7, J15.pin8, J15.pin9, J15.pin10, J15.pin11, J15.pin12, J15.pin13, J15.pin14, J15.pin15, J15.pin16, J15.pin17, J15.pin18, J15.pin19, J15.pin20, J15.pin21, J15.pin22, J15.pin23, J15.pin24
  N2: J16.pin1, J16.pin2, J17.pin1, J17.pin2, J17.pin3, J17.pin4, J17.pin5, J17.pin6, J17.pin7, J17.pin8, J17.pin9, J17.pin10, J17.pin11, J17.pin12, J17.pin13, J17.pin14, J17.pin15, J17.pin16, J17.pin17, J17.pin18, J17.pin19, J17.pin20, J17.pin21, J17.pin22, J17.pin23, J17.pin24
  N3: J18.pin1, J18.pin2, J19.pin1, J19.pin2, J19.pin3, J19.pin4, J19.pin5, J19.pin6, J19.pin7, J19.pin8, J19.pin9, J19.pin10, J19.pin11, J19.pin12, J19.pin13, J19.pin14, J19.pin15, J19.pin16, J19.pin17, J19.pin18, J19.pin19, J19.pin20, J19.pin21, J19.pin22, J19.pin23, J19.pin24
  N4: J20.pin1, J20.pin2, J21.pin1, J21.pin2, J21.pin3, J21.pin4, J21.pin5, J21.pin6, J21.pin7, J21.pin8, J21.pin9, J21.pin10, J21.pin11, J21.pin12, J21.pin13, J21.pin14, J21.pin15, J21.pin16, J21.pin17, J21.pin18, J21.pin19, J21.pin20, J21.pin21, J21.pin22, J21.pin23, J21.pin24
  N5: J22.pin1, J22.pin2, J23.pin1, J23.pin2, J23.pin3, J23.pin4, J23.pin5, J23.pin6, J23.pin7, J23.pin8, J23.pin9, J23.pin10, J23.pin11, J23.pin12, J23.pin13, J23.pin14, J23.pin15, J23.pin16, J23.pin17, J23.pin18, J23.pin19, J23.pin20, J23.pin21, J23.pin22, J23.pin23, J23.pin24

notes:
  GND
  +V2_out
  +V1_out
  +V_in
  VOLOUT
  Power Board V1.0 (SPCPB10)
  SteelsquidPiCon
  STEELSQUID.ORG
  A
  6
  7
  +3V3_out
  +5V_out
  ADJV2
  ADJV1
  +3V3_in
  +5V_in
  USB
  +V_out
  GPIO04
  GPIO26
  GPIO09
