# Fritzing sketch steelsquid_IO_v1_0 (saved by Fritzing 0.9.1b)
circuit board: 12cm x 10cm
breadboards: 1

parts:
  R_GPIO = double row female pin header, 40 pins [form="♀ (female)"]
  UART = male pin header, 2 pins [form="♂ (male)"]
  PCM = male pin header, 1 pin [form="♂ (male)"]
  GPIO = male pin header, 3 pins [form="♂ (male)"]
  GPIO_2 = male pin header, 4 pins [form="♂ (male)"]
  SPI = male pin header, 3 pins [form="♂ (male)"]
  GPIO_3 = male pin header, 5 pins [form="♂ (male)"]
  GPIO_4 = male pin header, 4 pins [form="♂ (male)"]
  SPI_2 = male pin header, 2 pins [form="♂ (male)"]
  10k = Resistor [tolerance=±5% resistance=220 package=THT]
  4k7 = Resistor [tolerance=±5% resistance=220 package=THT]
  4k7_2 = Resistor [tolerance=±5% resistance=220 package=THT]
  10k_2 = Resistor [tolerance=±5% resistance=220 package=THT]
  1N4007 = Rectifier Diode [part_number=1N4001 package="300 mil [THT]"]
  J60 = male pin header, 2 pins [form="♂ (male)"]
  J61 = screw terminal, 2 pins
  J62 = screw terminal, 2 pins
  UART140 = double row male pin header, 16 pins [form="♂ (male)"]
  UART142 = male pin header, 9 pins [form="♂ (male)"]
  UART147 = male pin header, 4 pins [form="♂ (male)"]
  UART148 = male pin header, 5 pins [form="♂ (male)"]
  UART149 = male pin header, 5 pins [form="♂ (male)"]
  560K = Resistor [tolerance=±5% resistance=220 package=THT]
  J104 = male pin header, 1 pin [form="♂ (male)"]
  MCP23020 = IC, DIP package, 20 pins [chip_label=IC]
  J105 = male pin header, 3 pins [form="♂ (male)"]
  J106 = male pin header, 3 pins [form="♂ (male)"]
  J107 = male pin header, 3 pins [form="♂ (male)"]
  J108 = male pin header, 3 pins [form="♂ (male)"]
  J109 = male pin header, 4 pins [form="♂ (male)"]
  J110 = male pin header, 4 pins [form="♂ (male)"]
  J111 = male pin header, 3 pins [form="♂ (male)"]
  J112 = male pin header, 3 pins [form="♂ (male)"]
  J113 = male pin header, 3 pins [form="♂ (male)"]
  J114 = male pin header, 3 pins [form="♂ (male)"]
  J116 = male pin header, 3 pins [form="♂ (male)"]
  J117 = male pin header, 1 pin [form="♂ (male)"]
  UART159 = male pin header, 4 pins [form="♂ (male)"]
  J118 = screw terminal, 2 pins
  UART161 = male pin header, 4 pins [form="♂ (male)"]
  ERROR3 = LED - 3mm [color="Orange (612nm)" package="3 mm [THT]"]
  C1 = Electrolytic Capacitor [capacitance=1µF package="100 mil [THT, electrolytic]"]  # not connected
  UART168 = male pin header, 2 pins [form="♂ (male)"]
  UART169 = male pin header, 2 pins [form="♂ (male)"]
  Q1 = NPN-Transistor [package="TO92 [THT]"]
  100k = Resistor [tolerance=±5% resistance=220 package=THT]
  UART170 = male pin header, 2 pins [form="♂ (male)"]
  UART139 = male pin header, 6 pins [form="♂ (male)"]
  UART181 = male pin header, 6 pins [form="♂ (male)"]
  UART180 = male pin header, 1 pin [form="♂ (male)"]
  UART179 = male pin header, 1 pin [form="♂ (male)"]
  UART130 = male pin header, 1 pin [form="♂ (male)"]
  UART129 = male pin header, 1 pin [form="♂ (male)"]
  UART185 = male pin header, 8 pins [form="♂ (male)"]  # not connected
  UART186 = male pin header, 8 pins [form="♂ (male)"]  # not connected
  UART171 = male pin header, 2 pins [form="♂ (male)"]
  J131 = male pin header, 1 pin [form="♂ (male)"]  # not connected
  J132 = male pin header, 1 pin [form="♂ (male)"]  # not connected
  S1 = Pushbutton [package=THT]
  ULN2803A = IC, DIP package, 18 pins [chip_label=IC]
  UART195 = male pin header, 9 pins [form="♂ (male)"]
  UART198 = male pin header, 2 pins [form="♂ (male)"]  # not connected
  UART199 = male pin header, 2 pins [form="♂ (male)"]  # not connected
  ERROR9 = LED - 3mm [color="Green (565nm)" package="3 mm [THT]"]
  ERROR10 = LED - 3mm [color="Red (635nm)" package="3 mm [THT]"]
  ERROR11 = LED - 3mm [color="Yellow (592nm)" package="3 mm [THT]"]
  ERROR12 = LED - 3mm [color="White (6500K)" package="3 mm [THT]"]
  UART200 = male pin header, 2 pins [form="♂ (male)"]
  UART201 = male pin header, 2 pins [form="♂ (male)"]
  UART202 = male pin header, 2 pins [form="♂ (male)"]
  UART203 = male pin header, 2 pins [form="♂ (male)"]
  S5 = Pushbutton [package=THT]
  S6 = Pushbutton [package=THT]
  S7 = Pushbutton [package=THT]
  S8 = Pushbutton [package=THT]
  S9 = Pushbutton [package=THT]
  UART204 = male pin header, 2 pins [form="♂ (male)"]
  ERROR13 = LED - 3mm [color="Blue (525nm)" package="3 mm [THT]"]
  UART206 = male pin header, 2 pins [form="♂ (male)"]
  ERROR15 = LED - 3mm [color="White (6500K)" package="3 mm [THT]"]
  UART207 = male pin header, 2 pins [form="♂ (male)"]
  ERROR16 = LED - 3mm [color="White (6500K)" package="3 mm [THT]"]
  UART208 = male pin header, 2 pins [form="♂ (male)"]
  ERROR17 = LED - 3mm [color="White (4500K)" package="3 mm [THT]"]
  DIP> = IC, DIP package, 12 pins [chip_label=DIP]
  J125 = male pin header, 6 pins [form="♂ (male)"]
  J133 = male pin header, 6 pins [form="♂ (male)"]
  J134 = male pin header, 6 pins [form="♂ (male)"]
  UART216 = male pin header, 3 pins [form="♂ (male)"]
  UART218 = male pin header, 3 pins [form="♂ (male)"]
  UART217 = male pin header, 5 pins [form="♂ (male)"]
  J135 = screw terminal, 2 pins
  J136 = double row male pin header, 6 pins [form="♂ (male)"]
  UART221 = male pin header, 5 pins [form="♂ (male)"]
  J115 = male pin header, 3 pins [form="♂ (male)"]
  UART222 = male pin header, 1 pin [form="♂ (male)"]  # not connected
  UART223 = male pin header, 1 pin [form="♂ (male)"]
  J119 = male pin header, 2 pins [form="♂ (male)"]
  J130 = male pin header, 4 pins [form="♂ (male)"]
  J123 = male pin header, 4 pins [form="♂ (male)"]
  J120 = male pin header, 4 pins [form="♂ (male)"]
  UART174 = male pin header, 1 pin [form="♂ (male)"]
  UART173 = male pin header, 1 pin [form="♂ (male)"]
  UART175 = male pin header, 1 pin [form="♂ (male)"]  # not connected
  UART144 = male pin header, 4 pins [form="♂ (male)"]
  UART143 = male pin header, 5 pins [form="♂ (male)"]
  UART224 = male pin header, 1 pin [form="♂ (male)"]  # not connected
  J122 = male pin header, 4 pins [form="♂ (male)"]
  J121 = male pin header, 4 pins [form="♂ (male)"]
  J139 = male pin header, 4 pins [form="♂ (male)"]
  UART155 = male pin header, 2 pins [form="♂ (male)"]
  UART156 = male pin header, 3 pins [form="♂ (male)"]
  UART151 = male pin header, 4 pins [form="♂ (male)"]
  UART150 = male pin header, 5 pins [form="♂ (male)"]
  UART225 = male pin header, 4 pins [form="♂ (male)"]
  J127 = screw terminal, 2 pins
  J129 = male pin header, 6 pins [form="♂ (male)"]
  Pad4 = Pad [width=2.63408348148148 height=4.65667607407407 connect=center]
  Pad5 = Pad [width=2.63408348148148 height=4.65667607407407 connect=center]  # not connected
  Pad7 = Pad [width=1.8 height=1.8 connect=center]
  Pad12 = Pad [width=1.8 height=1.8 connect=center]
  Pad13 = Pad [width=1.8 height=1.8 connect=center]
  Pad14 = Pad [width=1.8 height=1.8 connect=center]  # not connected
  Pad15 = Pad [width=1.8 height=1.8 connect=center]
  Pad16 = Pad [width=1.8 height=1.8 connect=center]
  Pad17 = Pad [width=2.4 height=2.4 connect=center]  # not connected
  Pad18 = Pad [width=2.4 height=2.4 connect=center]  # not connected
  Pad19 = Pad [width=2.4 height=2.4 connect=center]  # not connected
  Pad20 = Pad [width=2.4 height=2.4 connect=center]  # not connected
  Pad21 = Pad [width=1.8 height=1.8 connect=center]
  Pad22 = Pad [width=1.8 height=1.8 connect=center]
  Pad23 = Pad [width=1.8 height=1.8 connect=center]
  Pad24 = Pad [width=1.8 height=1.8 connect=center]
  Pad25 = Pad [width=1.8 height=1.8 connect=center]
  Pad26 = Pad [width=1.8 height=1.8 connect=center]
  Pad27 = Pad [width=1.8 height=1.8 connect=center]
  Pad29 = Pad [width=13 height=3.2 connect=center]  # not connected
  Pad30 = Pad [width=3.2 height=16 connect=center]  # not connected
  Pad31 = Pad [width=5.17404585185186 height=3.66887007407408 connect=center]  # not connected
  Pad32 = Pad [width=4.36591192592594 height=2.5 connect=center]  # not connected
  Pad33 = Pad [width=2.6 height=11 connect=center]  # not connected
  Pad34 = Pad [width=4 height=3.66887007407408 connect=center]  # not connected
  Pad35 = Pad [width=18.3444162222222 height=3.1 connect=center]  # not connected
  Pad36 = Pad [width=2 height=8 connect=center]  # not connected
  Pad37 = Pad [width=3.01033274074074 height=2.35182362962963 connect=center]  # not connected
  Pad38 = Pad [width=13 height=2 connect=center]  # not connected
  Pad39 = Pad [width=3.01033274074074 height=3 connect=center]  # not connected
  Pad41 = Pad [width=10 height=3.1 connect=center]  # not connected
  Pad42 = Pad [width=6.95954355555556 height=7 connect=center]  # not connected
  Pad43 = Pad [width=19 height=3.1 connect=center]  # not connected
  J140 = male pin header, 3 pins [form="♂ (male)"]
  J141 = male pin header, 3 pins [form="♂ (male)"]
  Pad11 = Pad [width=1.8 height=1.8 connect=center]
  Pad10 = Pad [width=1.8 height=1.8 connect=center]
  Pad9 = Pad [width=1.8 height=1.8 connect=center]  # not connected
  47 = Resistor [tolerance=±5% resistance=56 package=THT]
  UART227 = double row male pin header, 10 pins [form="♂ (male)"]
  UART229 = male pin header, 2 pins [form="♂ (male)"]
  UART228 = male pin header, 1 pin [form="♂ (male)"]
  UART230 = male pin header, 3 pins [form="♂ (male)"]
  R5 = Resistor [tolerance=±5% resistance=2.2k package="0805 [SMD]"]
  R6 = Resistor [tolerance=±5% resistance=2.2k package="0805 [SMD]"]
  UART232 = male pin header, 3 pins [form="♂ (male)"]
  UART234 = male pin header, 2 pins [form="♂ (male)"]
  UART219 = male pin header, 6 pins [form="♂ (male)"]
  UART220 = male pin header, 6 pins [form="♂ (male)"]
  UART226 = male pin header, 8 pins [form="♂ (male)"]
  UART235 = male pin header, 3 pins [form="♂ (male)"]
  UART237 = double row male pin header, 6 pins [form="♂ (male)"]
  UART238 = male pin header, 3 pins [form="♂ (male)"]
  Pad44 = Pad [width=1.8 height=8 connect=center]  # not connected
  Pad45 = Pad [width=6.28410111111112 height=2.069592 connect=center]  # not connected
  Pad46 = Pad [width=3.5 height=1.8 connect=center]  # not connected
  Pad47 = Pad [width=3.28311933333333 height=6.09156911111113 connect=center]  # not connected
  C2 = Electrolytic Capacitor [capacitance=1µF voltage=50V package="100 mil [THT, electrolytic]"]
  Pad51 = Pad [width=1.8 height=1.8 connect=center]  # not connected
  ERROR2 = LED - 3mm [color="White (4500K)" package="3 mm [THT]"]
  Pad54 = Pad [width=1.8 height=1.8 connect=center]  # not connected
  Pad55 = Pad [width=1.90591157777777 height=8.56444725925926 connect=center]  # not connected
  Pad56 = Pad [width=3.01033274074074 height=2.2 connect=center]  # not connected
  Pad57 = Pad [width=1.6 height=9 connect=center]  # not connected
  Pad58 = Pad [width=3.01033274074074 height=2.35182362962963 connect=center]  # not connected
  Pad59 = Pad [width=3.01033274074074 height=3 connect=center]  # not connected
  UART239 = male pin header, 2 pins [form="♂ (male)"]

nets:
  N1: R_GPIO.pin1, R_GPIO.pin9, UART142.pin1, MCP23020.pin1, UART159.pin4, J118.pin1, J118.pin2, UART168.pin2, UART170.pin1, UART171.pin2, UART216.pin1, UART216.pin2, UART216.pin3, UART218.pin1, UART218.pin2, UART218.pin3, UART217.pin1, UART217.pin2, UART217.pin3, UART217.pin4, UART217.pin5, J120.pin1, J120.pin2, J120.pin3, J120.pin4, UART143.pin1, UART143.pin5, UART155.pin2, UART156.pin1, UART150.pin1, UART235.pin1, UART235.pin2, UART235.pin3, UART238.pin1, UART238.pin2, UART238.pin3, ERROR2.anode
  N2: R_GPIO.pin2, UART149.pin3, MCP23020.pin13, UART159.pin1, UART143.pin2, J122.pin1, J122.pin2, J122.pin3, J122.pin4, UART156.pin2, UART150.pin4, UART227.pin1, UART227.pin2, UART227.pin3, UART227.pin4, UART227.pin5, UART237.pin1, UART237.pin2, UART237.pin3
  N3: R_GPIO.pin3, UART149.pin2, MCP23020.pin11, UART159.pin2, UART143.pin3, J121.pin1, J121.pin2, J121.pin3, J121.pin4, UART156.pin3, UART150.pin3, UART227.pin6, UART227.pin7, UART227.pin8, UART227.pin9, UART227.pin10, UART237.pin4, UART237.pin5, UART237.pin6
  N4: R_GPIO.pin4, GPIO_2.pin1
  N5: R_GPIO.pin6, GPIO_2.pin2
  N6: R_GPIO.pin7, GPIO_2.pin3
  N7: R_GPIO.pin8, GPIO_2.pin4
  N8: R_GPIO.pin10, SPI.pin1
  N9: R_GPIO.pin11, SPI.pin2
  N10: R_GPIO.pin12, SPI.pin3
  N11: R_GPIO.pin13, UART168.pin1, ERROR2.cathode
  N12: R_GPIO.pin15, GPIO_3.pin1
  N13: R_GPIO.pin16, GPIO_3.pin2, UART142.pin9
  N14: R_GPIO.pin17, GPIO_3.pin3, UART142.pin8
  N15: R_GPIO.pin18, GPIO_3.pin4, UART142.pin7
  N16: R_GPIO.pin19, GPIO_3.pin5, UART142.pin6
  N17: R_GPIO.pin21, GPIO_4.pin4, UART142.pin5
  N18: R_GPIO.pin22, GPIO_4.pin3, UART142.pin4
  N19: R_GPIO.pin23, GPIO_4.pin2, UART142.pin3
  N20: R_GPIO.pin25, GPIO_4.pin1, UART142.pin2
  N21: R_GPIO.pin26, J136.pin1, J136.pin2, J136.pin3, J136.pin4, J136.pin5, J136.pin6
  N22: R_GPIO.pin28, SPI_2.pin2
  N23: R_GPIO.pin29, SPI_2.pin1
  N24: R_GPIO.pin30, GPIO.pin3
  N25: R_GPIO.pin32, GPIO.pin2
  N26: R_GPIO.pin33, GPIO.pin1
  N27: R_GPIO.pin35, PCM.pin1
  N28: R_GPIO.pin36, UART.pin2, J119.pin2
  N29: R_GPIO.pin37, UART.pin1, J119.pin1
  N30: R_GPIO.pin39, R_GPIO.pin40, 10k.Pin_1, 4k7.Pin_1, 10k_2.Pin_1, 1N4007.cathode, J62.pin1, J62.pin2, UART140.pin1, UART140.pin2, UART140.pin3, UART140.pin4, UART140.pin5, UART140.pin6, UART140.pin7, UART140.pin8, UART140.pin9, UART140.pin10, UART140.pin11, UART140.pin12, UART140.pin13, UART140.pin14, UART140.pin15, UART140.pin16, J104.pin1, J117.pin1, UART223.pin1, J123.pin1, J123.pin2, J123.pin3, J123.pin4, UART229.pin2, C2.+
  N31: 4k7.Pin_0, Q1.E
  N32: 4k7_2.Pin_0, Q1.B
  N33: 4k7_2.Pin_1, UART169.pin2, 47.Pin_0
  N34: J60.pin1, 560K.Pin_1, J130.pin1, J130.pin2, J130.pin3, J130.pin4, J129.pin1, J129.pin2, J129.pin3, J129.pin4, J129.pin5, J129.pin6, UART228.pin1, UART234.pin2, UART239.pin2
  N35: J61.pin1, J61.pin2, UART139.pin1, UART139.pin2, UART139.pin3, UART139.pin4, UART139.pin5, UART139.pin6, UART129.pin1
  N36: UART147.pin1, UART148.pin2
  N37: UART147.pin2, UART148.pin3
  N38: UART147.pin3, UART148.pin4
  N39: UART147.pin4, UART148.pin5
  N40: UART148.pin1, Pad22.pad, Pad27.pad
  N41: UART149.pin1, UART170.pin2
  N42: 560K.Pin_0, 100k.Pin_0, UART144.pin1
  N43: MCP23020.pin2, J105.pin3
  N44: MCP23020.pin3, J105.pin2
  N45: MCP23020.pin4, MCP23020.pin5, MCP23020.pin6
  N46: MCP23020.pin7, J105.pin1
  N47: MCP23020.pin8, J106.pin3
  N48: MCP23020.pin9, J106.pin2
  N49: MCP23020.pin10, J106.pin1
  N50: MCP23020.pin12, J107.pin1
  N51: MCP23020.pin14, J107.pin2
  N52: MCP23020.pin15, J107.pin3
  N53: MCP23020.pin16, J108.pin1
  N54: MCP23020.pin18, J108.pin2
  N55: MCP23020.pin19, J108.pin3
  N56: MCP23020.pin20, Pad15.pad, Pad16.pad
  N57: J109.pin1, J109.pin2, J109.pin3, J109.pin4, J112.pin1, J112.pin2, J112.pin3
  N58: J110.pin1, J110.pin2, J110.pin3, J110.pin4, J114.pin1, J114.pin2, J114.pin3
  N59: J111.pin1, J111.pin2, J111.pin3
  N60: J113.pin1, J113.pin2, J113.pin3
  N61: J116.pin1, J116.pin2, J116.pin3
  N62: UART161.pin1, UART151.pin1
  N63: UART161.pin2, UART151.pin2
  N64: UART161.pin3, UART151.pin3
  N65: UART161.pin4, UART151.pin4
  N66: ERROR3.cathode, UART169.pin1
  N67: ERROR3.anode, 47.Pin_1
  N68: UART181.pin1, UART181.pin2, UART181.pin3, UART181.pin4, UART181.pin5, UART181.pin6, UART180.pin1, J127.pin1, J127.pin2
  N69: UART179.pin1, UART130.pin1, UART239.pin1
  N70: S1.leg0, J140.pin1
  N71: S1.leg1, S5.leg1, S6.leg1, S7.leg1, S8.leg1, S9.leg1, J133.pin1, J133.pin2, J133.pin3, J133.pin4, J133.pin5, J133.pin6
  N72: ULN2803A.pin9, UART225.pin1, UART225.pin2, UART225.pin3, UART225.pin4, Pad7.pad, Pad21.pad
  N73: ULN2803A.pin10, UART195.pin9
  N74: ULN2803A.pin11, UART195.pin8
  N75: ULN2803A.pin12, UART195.pin7
  N76: ULN2803A.pin13, UART195.pin6
  N77: ULN2803A.pin14, UART195.pin5
  N78: ULN2803A.pin15, UART195.pin4
  N79: ULN2803A.pin16, UART195.pin3
  N80: ULN2803A.pin17, UART195.pin2
  N81: ULN2803A.pin18, UART195.pin1
  N82: ERROR9.cathode, UART200.pin2
  N83: ERROR9.anode, UART200.pin1
  N84: ERROR10.cathode, UART201.pin2
  N85: ERROR10.anode, UART201.pin1, R5.Pin_1
  N86: ERROR11.cathode, UART202.pin2
  N87: ERROR11.anode, UART202.pin1, R6.Pin_1
  N88: ERROR12.cathode, UART203.pin2
  N89: ERROR12.anode, UART203.pin1
  N90: S5.leg0, J140.pin2
  N91: S6.leg0, J140.pin3
  N92: S7.leg0, J141.pin1
  N93: S8.leg0, J141.pin2
  N94: S9.leg0, J141.pin3
  N95: UART204.pin1, ERROR13.cathode, UART207.pin2, ERROR16.cathode, UART208.pin1, ERROR17.cathode, DIP>.pin1, DIP>.pin2, DIP>.pin3, DIP>.pin4, DIP>.pin5, DIP>.pin6, J134.pin1, J134.pin2, J134.pin3, J134.pin4, J134.pin5, J134.pin6
  N96: UART204.pin2, ERROR13.anode
  N97: UART206.pin1, ERROR15.anode
  N98: UART206.pin2, ERROR15.cathode
  N99: UART207.pin1, ERROR16.anode
  N100: UART208.pin2, ERROR17.anode
  N101: DIP>.pin7, J125.pin1
  N102: DIP>.pin8, J125.pin2
  N103: DIP>.pin9, J125.pin3
  N104: DIP>.pin10, J125.pin4
  N105: DIP>.pin11, J125.pin5
  N106: DIP>.pin12, J125.pin6
  N107: J135.pin1, J135.pin2, UART219.pin1, UART219.pin2, UART219.pin3, UART219.pin4, UART219.pin5, UART219.pin6, UART220.pin1, UART220.pin2, UART220.pin3, UART220.pin4, UART220.pin5, UART220.pin6, UART226.pin1, UART226.pin2, UART226.pin3, UART226.pin4, UART226.pin5, UART226.pin6, UART226.pin7, UART226.pin8
  N108: UART221.pin1, UART221.pin2, UART221.pin3, UART221.pin4, UART221.pin5
  N109: J115.pin1, J115.pin2, J115.pin3
  N110: UART174.pin1, UART229.pin1
  N111: UART173.pin1, UART234.pin1
  N112: UART144.pin2, UART232.pin1
  N113: UART144.pin3, UART232.pin2
  N114: UART144.pin4, UART232.pin3
  N115: J139.pin1, J139.pin2, J139.pin3, J139.pin4
  N116: Pad4.pad, Pad11.pad, Pad10.pad
  N117: Pad12.pad, Pad13.pad
  N118: Pad23.pad, Pad24.pad
  N119: Pad25.pad, Pad26.pad
  N120: UART230.pin1, UART230.pin2, UART230.pin3

notes:
  +3V3
  GPIO2_I2C_SDA
  GPIO3_I2C_SCL
  GPIO4
  GND
  GPIO17
  GPIO27
  GPIO22
  GPIO10_SPI_MOSI
  GPIO9_SPI_MISO
  NC
  GPIO5
  GPIO6
  GPIO13
  GPIO19
  GPIO26
  GPIO21
  GPIO20
  GPIO16
  GPIO12
  GPIO24
  GPIO23
  +5V
  GPIO11_SPI_CLK
  GPIO7_SPI_CE1
  GPIO8_SPI_CE0
  GPIO25
  GPIO18_PCM_CLK
  GPIO15_UART_RXD
  GPIO14_UART_TXD
  -----------SDA-----------
  -----------SCL-----------
  5V
  3_18_PCM
  2_15_RXD
  1_14_TXD
  6_25
  5_24
  4_23
  12_21
  11_20
  16
  9-12
  10-
  16_22
  15_27
  14_17
  13_4
  MISO_18_9
  CLK_19_11
  24_26
  23_19
  22_13
  21_6
  20_5
  Main Power IN
  Screw terminal
  Main Power OUT
  SRD-05VDC-SL-C
  V
  SIG
  V_IN
  V_OUT
  TRIM
  CV
  TH
  DI
  +
  RE
  OU
  TR
  -
  TLC555CP
  C
  500KΩ
  10uF
  100nF
  10nF
  100uF
  _
  BC547B
  <OFF_SIG
  7_8_CE0
  8_7_CE1
  OFF
  POWER
  Show IP
  Push
  Input
  POWER_ON
  ON
  +IN
  DELAY_POWER_OFF
  [-]
  V-Reg (5V)
  +OUT
  Bypass
  Use 5V reg
  min/2V8><10V/max
  Adaf. I2C lev con
  V-Reg (ADJ)
  GND->
  3V3 side
  Adafruit 8C lev con
  POWERING
  23-19
  21-06
  24-26
  22-13
  10-16
  12-21
  11-20
  10_16
  DAC
  Vo3
  Vo1
  3
  Vo2
  Vo0
  1
  2
  SDA
  SCL
  4
  3.3>5.5V
  SRV
  S11
  S10
  S9
  S8
  S7
  S6
  S5
  S3
  S4
  S2
  AD0
  AD1
  AD2
  S1
  S0
  3V3
  5
  6
  7
  9
  11
  10
  12
  8
  +SRV
  3>5V
  Solder on top
  TRIM_2
  TRIM_1
  V_Reg_5V
  1N4007
  MCP4728
  I2C_SDA
  I2C_SCL
  ---SDA---
  -----SCL-
  ADDR
  MOSI_17_10
  6_PIN_DIP
  V_ADJ_1
  V_ADJ_2
  GPIO_3V3
  MP1584EN Ajd Reg Mod
  BUTTON
  Max 40V/500mA
  40V/500mA
  OLED_0.96"
  SERVO12C(HT)
  POWER_OFF
  SUM
  com
  COM
  0
  A0 A1 A2
  5-
  PI_GPIO
  XGPIO
  GPIO
  INFO
  LOW_BAT
  OK
  ERR
  NET
  ---LED---
  BT
  BUTTONS
  MCP9700T
  MCP23017
  ULN2803A
  UART
  TXD
  RXD
  8V to 26V IN
  -IN
  A3
  A2
  A1
  A0
  MP1584EN Ajd Reg Mod (5V)
  -OUT
  MPU-6050
  SparkFun
  Adafruit
  ADC_1
  SERVO
  I2C
  ADS1015
  5V side
  Main Power Relay
  SteelsquidIO_v1_0
  steelsquid.org
  Mounting
  plate
  Mounting plate
  hole
  Raspberry PI
  IN1
  IN2
  IN3
  IN4
  IN5
  IN6
  IN7
  IN8
  OU2
  OU5
  OU8
  OU6
  OU4
  OU1
  OU3
  OU7
  CONTROLLER
  DIP>
  VOLT
  <GPIO_5V
  PI GPIO
  I2C_ADD=3C
  Adafruit ADS1015 I2C=49
  SparkFun MPU-6050 I2C=69
  ADS1015    I2C=48
  I2C=48
  MCP4728 I2C=61
  I2C=28
  MCP23017 I2C=20
  MCP23017 I2C=27
  MCP23017 I2C=26
  I2C_ADD=49
  PIN=A3
  A>
  B>
  TILT
  OLED_0.96: I2C_ADD=3C
  VOLT: ADS1015 I2C_ADD=49 PIN=A3
  SERVO_CON: SERVO12C(HT) I2C_ADD=28 PIN=S0-S11
  POWERING_OFF: MCP23017 I2C_ADD=26 PIN=B7
  BUTTON: MCP23017 I2C_ADD=26 PIN=B0-B5
  SUM: MCP23017 I2C_ADD=26 PIN=B6
  DIP: MCP23017 I2C_ADD=26 PIN=A2-A7
  BT: MCP23017 I2C_ADD=27 PIN=A6
  LED_1: MCP23017 I2C_ADD=27 PIN=A7
  LED_2: MCP23017 I2C_ADD=26 PIN=A0
  LED_3: MCP23017 I2C_ADD=26 PIN=A1
  OK: MCP23017 I2C_ADD=27 PIN=A3
  ERR: MCP23017 I2C_ADD=27 PIN=A4
  NET: MCP23017 I2C_ADD=27 PIN=A5
  LOW_BAT: MCP23017 I2C_ADD=27 PIN=A2
  POWER_OFF: MCP23017 I2C_ADD=27 PIN=A1
  INFO: MCP23017 I2C_ADD=27 PIN=A0
  POWER: MCP23017 I2C_ADD=27 PIN=B0-B7
  XGPIO: MCP23017 I2C_ADD=20 PIN=A0-B7
  DAC: MCP4728 I2C_ADD=61 PIN=Vo0-Vo3
  ADC_1: ADS1015 I2C_ADD=48 PIN=A0-A3
  ADC_2: ADS1015 I2C_ADD=49 PIN=A0-A2
  TILT: MPU-6050 I2C_ADD=69
  <SDM=47ohm
  BYPASS_5V_REG
  <
  <5V_REG
  I=GPIO
  G=GND
  I  G
  I
  G
  I   G
  G  I
  I2C=49
  ADC_2
  USE_V_ADJ>
  Bypass 5V Reg
  In must be 5V
  SteelsquidIO
  2015-04-10
  v1_0
  DELAY_POWER_OFF: 0 to 50s
  ADJ
