# Fritzing sketch steelsquid_PIIO_v1_0 (saved by Fritzing 0.9.2b)
circuit board: 12cm x 10cm
breadboards: 1

parts:
  R_GPIO2 = double row female pin header, 40 pins [form="♀ (female)"]
  SPI1 = male pin header, 2 pins [form="♂ (male)"]
  UART1 = male pin header, 2 pins [form="♂ (male)"]
  PCM1 = male pin header, 1 pin [form="♂ (male)"]
  GPIO1 = male pin header, 3 pins [form="♂ (male)"]
  GPIO2 = male pin header, 4 pins [form="♂ (male)"]
  SPI2 = male pin header, 3 pins [form="♂ (male)"]
  GPIO3 = male pin header, 5 pins [form="♂ (male)"]
  GPIO4 = male pin header, 4 pins [form="♂ (male)"]
  J61 = male pin header, 2 pins [form="♂ (male)"]
  UART227 = male pin header, 10 pins [form="♂ (male)"]
  UART228 = male pin header, 8 pins [form="♂ (male)"]
  UART233 = male pin header, 1 pin [form="♂ (male)"]
  UART234 = male pin header, 1 pin [form="♂ (male)"]
  UART235 = male pin header, 1 pin [form="♂ (male)"]  # not connected
  UART236 = male pin header, 1 pin [form="♂ (male)"]  # not connected
  UART237 = male pin header, 2 pins [form="♂ (male)"]
  UART238 = male pin header, 2 pins [form="♂ (male)"]
  UART242 = male pin header, 1 pin [form="♂ (male)"]
  UART243 = male pin header, 1 pin [form="♂ (male)"]
  UART244 = male pin header, 1 pin [form="♂ (male)"]  # not connected
  UART245 = male pin header, 1 pin [form="♂ (male)"]  # not connected
  UART246 = male pin header, 2 pins [form="♂ (male)"]
  UART247 = male pin header, 4 pins [form="♂ (male)"]
  U1 = 556 [package=dil14]
  220uF_16V = Capacitor Polarized [package=cpol-radial-100uf-25v]
  220uF_16V_2 = Capacitor Polarized [package=cpol-radial-100uf-25v]
  100nF = Ceramic Capacitor [capacitance=100nF voltage=50V package="200 mil [THT, multilayer]"]
  10nF = Ceramic Capacitor [capacitance=10nF voltage=50V package="200 mil [THT, multilayer]"]
  10nF_2 = Ceramic Capacitor [capacitance=10nF voltage=50V package="200 mil [THT, multilayer]"]
  10kΩ = Resistor [tolerance=±1% resistance=10k package=THT]
  10kΩ_2 = Resistor [tolerance=±1% resistance=10k package=THT]
  BC547B = NPN-Transistor [package="TO92 [THT]"]
  10nF_3 = Ceramic Capacitor [capacitance=10nF voltage=50V package="200 mil [THT, multilayer]"]
  4k7Ω = Resistor [tolerance=±1% resistance=4.7k package=THT]
  270kΩ = Resistor [tolerance=±1% resistance=270k package=THT]
  UART255 = double row male pin header, 8 pins [form="♂ (male)"]
  UART256 = double row male pin header, 8 pins [form="♂ (male)"]
  J133 = screw terminal, 2 pins
  J134 = screw terminal, 2 pins
  10nF_4 = Ceramic Capacitor [capacitance=10nF voltage=50V package="200 mil [THT, multilayer]"]
  UART226 = male pin header, 10 pins [form="♂ (male)"]
  IC1 = H-Bridge [package=THT]
  IC2 = IC, DIP package, 20 pins [chip_label=IC]
  UART263 = male pin header, 2 pins [form="♂ (male)"]
  LED_6 = LED - 3mm [color="White (4500K)" package="3 mm [THT]"]
  UART264 = male pin header, 2 pins [form="♂ (male)"]
  LED_5 = LED - 3mm [color="White (4500K)" package="3 mm [THT]"]
  UART265 = male pin header, 2 pins [form="♂ (male)"]
  LED_4 = LED - 3mm [color="White (4500K)" package="3 mm [THT]"]
  UART266 = male pin header, 2 pins [form="♂ (male)"]
  LED_3 = LED - 3mm [color="White (4500K)" package="3 mm [THT]"]
  UART267 = male pin header, 2 pins [form="♂ (male)"]
  LED_2 = LED - 3mm [color="White (4500K)" package="3 mm [THT]"]
  UART268 = male pin header, 2 pins [form="♂ (male)"]
  LED_1 = LED - 3mm [color="White (4500K)" package="3 mm [THT]"]
  UART269 = male pin header, 2 pins [form="♂ (male)"]
  100nF_2 = Ceramic Capacitor [capacitance=100nF voltage=50V package="200 mil [THT, multilayer]"]
  1uF = Tantalum Capacitor [capacitance=1μF voltage=50V package="100 mil [THT, tantalum]"]
  10uF = Tantalum Capacitor [capacitance=10µF voltage=16V package="100 mil [THT, tantalum]"]
  10uF_2 = Tantalum Capacitor [capacitance=10µF voltage=16V package="100 mil [THT, tantalum]"]
  UART273 = double row male pin header, 8 pins [form="♂ (male)"]
  UART274 = double row male pin header, 8 pins [form="♂ (male)"]
  J137 = screw terminal, 2 pins
  J138 = screw terminal, 2 pins
  UART275 = double row male pin header, 8 pins [form="♂ (male)"]
  UART276 = double row male pin header, 8 pins [form="♂ (male)"]
  J139 = screw terminal, 2 pins
  J140 = screw terminal, 2 pins
  J142 = screw terminal, 2 pins
  UART277 = double row male pin header, 8 pins [form="♂ (male)"]
  10uF_3 = Tantalum Capacitor [capacitance=10µF voltage=16V package="100 mil [THT, tantalum]"]
  J146 = male pin header, 1 pin [form="♂ (male)"]
  MCP23021 = IC, DIP package, 20 pins [chip_label=IC]
  J147 = male pin header, 3 pins [form="♂ (male)"]
  J148 = male pin header, 3 pins [form="♂ (male)"]
  J149 = male pin header, 3 pins [form="♂ (male)"]
  J150 = male pin header, 3 pins [form="♂ (male)"]
  J151 = male pin header, 4 pins [form="♂ (male)"]
  J152 = male pin header, 4 pins [form="♂ (male)"]
  J153 = male pin header, 3 pins [form="♂ (male)"]
  J154 = male pin header, 3 pins [form="♂ (male)"]
  J155 = male pin header, 3 pins [form="♂ (male)"]
  J156 = male pin header, 3 pins [form="♂ (male)"]
  J158 = male pin header, 3 pins [form="♂ (male)"]
  J159 = male pin header, 1 pin [form="♂ (male)"]
  100nF_3 = Ceramic Capacitor [capacitance=100nF voltage=50V package="200 mil [THT, multilayer]"]
  J160 = male pin header, 1 pin [form="♂ (male)"]  # not connected
  J161 = male pin header, 1 pin [form="♂ (male)"]  # not connected
  UART278 = male pin header, 2 pins [form="♂ (male)"]
  BT_ON = LED - 3mm [color="Blue (470nm)" package="3 mm [THT]"]
  UART279 = male pin header, 2 pins [form="♂ (male)"]
  NET = LED - 3mm [color="Yellow (595nm)" package="3 mm [THT]"]
  UART281 = male pin header, 2 pins [form="♂ (male)"]
  POWER_IS_ON = LED - 3mm [color="Blue (505nm)" package="3 mm [THT]"]
  UART282 = male pin header, 2 pins [form="♂ (male)"]
  LOW_BAT = LED - 3mm [color="Red (660nm)" package="3 mm [THT]"]
  UART283 = male pin header, 2 pins [form="♂ (male)"]
  POWERING_OFF = LED - 3mm [color="Orange (612nm)" package="3 mm [THT]"]
  47Ω = Resistor [tolerance=±1% resistance=47 package=THT]
  47Ω_2 = Resistor [tolerance=±1% resistance=47 package=THT]
  UART284 = male pin header, 2 pins [form="♂ (male)"]
  UART285 = male pin header, 2 pins [form="♂ (male)"]
  OK = LED - 3mm [color="Green (565nm)" package="3 mm [THT]"]
  ERROR = LED - 3mm [color="Red (635nm)" package="3 mm [THT]"]
  DIP_SWITCH = IC, DIP package, 12 pins [chip_label=DIP_SWITCH]
  UART286 = male pin header, 6 pins [form="♂ (male)"]
  UART287 = male pin header, 6 pins [form="♂ (male)"]
  S17 = Momentary Switch [package=ksa_sealed_tac_switch]
  S18 = Momentary Switch [package=ksa_sealed_tac_switch]
  J165 = male pin header, 2 pins [form="♂ (male)"]
  J167 = male pin header, 2 pins [form="♂ (male)"]
  S19 = Pushbutton [package=THT]
  S20 = Pushbutton [package=THT]
  S21 = Pushbutton [package=THT]
  S22 = Pushbutton [package=THT]
  S23 = Pushbutton [package=THT]
  S24 = Pushbutton [package=THT]
  J168 = male pin header, 3 pins [form="♂ (male)"]
  J169 = male pin header, 3 pins [form="♂ (male)"]
  J170 = male pin header, 3 pins [form="♂ (male)"]
  J185 = male pin header, 3 pins [form="♂ (male)"]
  100nF_4 = Ceramic Capacitor [capacitance=100nF voltage=50V package="200 mil [THT, multilayer]"]
  10uF_4 = Tantalum Capacitor [capacitance=10µF voltage=16V package="100 mil [THT, tantalum]"]
  100nF_5 = Ceramic Capacitor [capacitance=100nF voltage=50V package="200 mil [THT, multilayer]"]
  UART293 = male pin header, 4 pins [form="♂ (male)"]
  UART280 = male pin header, 7 pins [form="♂ (male)"]  # not connected
  560kΩ = Resistor [tolerance=±1% resistance=560k package=THT]
  75kΩ = Resistor [tolerance=±1% resistance=75k package=THT]
  10uF_5 = Tantalum Capacitor [capacitance=10µF voltage=16V package="100 mil [THT, tantalum]"]
  ULN2803A1 = IC, DIP package, 18 pins [chip_label=IC]
  UART297 = male pin header, 9 pins [form="♂ (male)"]
  UART240 = double row male pin header, 12 pins [form="♂ (male)"]
  UART272 = male pin header, 6 pins [form="♂ (male)"]
  UART271 = male pin header, 6 pins [form="♂ (male)"]
  IC10 = IC, DIP package, 28 pins [chip_label=IC]
  J189 = male pin header, 8 pins [form="♂ (male)"]
  100nF_6 = Ceramic Capacitor [capacitance=100nF voltage=50V package="200 mil [THT, multilayer]"]
  10uF_6 = Tantalum Capacitor [capacitance=10µF voltage=16V package="100 mil [THT, tantalum]"]
  100nF_7 = Ceramic Capacitor [capacitance=100nF voltage=50V package="200 mil [THT, multilayer]"]
  10kΩ_3 = Resistor [tolerance=±1% resistance=10k package=THT]
  10kΩ_4 = Resistor [tolerance=±1% resistance=10k package=THT]
  S25 = Momentary Switch [package=ksa_sealed_tac_switch]
  47Ω_3 = Resistor [tolerance=±1% resistance=47 package=THT]
  47Ω_4 = Resistor [tolerance=±1% resistance=47 package=THT]
  56Ω = Resistor [tolerance=±1% resistance=56 package=THT]
  IC5 = IC, DIP package, 28 pins [chip_label=IC]
  J157 = male pin header, 3 pins [form="♂ (male)"]
  GPIO5 = female pin header, 4 pins [form="♀ (female)"]
  UART300 = male pin header, 10 pins [form="♂ (male)"]
  UART291 = male pin header, 5 pins [form="♂ (male)"]
  UART292 = male pin header, 5 pins [form="♂ (male)"]
  10uF_7 = Tantalum Capacitor [capacitance=10µF voltage=16V package="100 mil [THT, tantalum]"]
  10uF_8 = Tantalum Capacitor [capacitance=10µF voltage=16V package="100 mil [THT, tantalum]"]
  SPI3 = male pin header, 2 pins [form="♂ (male)"]
  SPI4 = male pin header, 2 pins [form="♂ (male)"]
  10uF_9 = Tantalum Capacitor [capacitance=10µF voltage=16V package="100 mil [THT, tantalum]"]
  J190 = male pin header, 3 pins [form="♂ (male)"]
  1N4007 = Diode [package=diode-1n4001]
  10uF_10 = Tantalum Capacitor [capacitance=10µF voltage=16V package="100 mil [THT, tantalum]"]
  UART301 = male pin header, 7 pins [form="♂ (male)"]
  UART302 = male pin header, 7 pins [form="♂ (male)"]
  100nF_8 = Ceramic Capacitor [capacitance=100nF voltage=50V package="200 mil [THT, multilayer]"]
  10uF_50V = Tantalum Capacitor [capacitance=10µF voltage=50V package="100 mil [THT, tantalum]"]
  FUSE = Resettable Fuse PTC [package=ptc]
  FUSE_2 = Resettable Fuse PTC [package=ptc]
  100uF = Electrolytic Capacitor [capacitance=100µF voltage=25V package="100 mil [THT, electrolytic]"]
  UART303 = female pin header, 2 pins [form="♀ (female)"]
  UART304 = female pin header, 3 pins [form="♀ (female)"]
  430Ω = Resistor [tolerance=±1% resistance=430 package=THT]
  1N4007_2 = Rectifier Diode [part_number=1N4001 package="300 mil [THT]"]
  560kΩ_2 = Resistor [tolerance=±1% resistance=560k package=THT]
  100nF_9 = Ceramic Capacitor [capacitance=100nF voltage=50V package="200 mil [THT, multilayer]"]
  UART305 = male pin header, 4 pins [form="♂ (male)"]

nets:
  N1: R_GPIO2.pin1, R_GPIO2.pin2, UART227.pin1, UART237.pin2, UART238.pin1, U1.RST, U1.RST2, U1.VCC, 220uF_16V_2.+, 100nF.0, 10kΩ.Pin_1, 10kΩ_2.Pin_1, 4k7Ω.Pin_1, IC1.VCC1, 100nF_2.1, 10uF_2.+, UART273.pin1, UART273.pin2, UART273.pin3, UART273.pin4, UART273.pin5, UART273.pin6, UART273.pin7, UART273.pin8, UART274.pin1, UART274.pin2, UART274.pin3, UART274.pin4, UART274.pin5, UART274.pin6, UART274.pin7, UART274.pin8, J137.pin1, J137.pin2, J138.pin1, J138.pin2, 10uF_3.+, J146.pin1, J159.pin1, 10uF_8.+, 1N4007.C, 10uF_10.+, 560kΩ_2.Pin_0
  N2: R_GPIO2.pin4, UART1.pin1, UART226.pin2, UART300.pin2
  N3: R_GPIO2.pin5, UART1.pin2, UART226.pin3, UART300.pin3
  N4: R_GPIO2.pin6, PCM1.pin1, UART226.pin4, UART300.pin4
  N5: R_GPIO2.pin8, GPIO1.pin1, UART226.pin5, UART300.pin5
  N6: R_GPIO2.pin9, GPIO1.pin2, UART226.pin6, UART300.pin6
  N7: R_GPIO2.pin11, GPIO1.pin3, UART226.pin7, UART300.pin7
  N8: R_GPIO2.pin12, SPI1.pin1, UART226.pin8, UART300.pin8
  N9: R_GPIO2.pin13, SPI1.pin2, UART226.pin9, UART300.pin9
  N10: R_GPIO2.pin16, GPIO4.pin1
  N11: R_GPIO2.pin18, GPIO4.pin2
  N12: R_GPIO2.pin19, GPIO4.pin3
  N13: R_GPIO2.pin20, GPIO4.pin4
  N14: R_GPIO2.pin22, GPIO3.pin5, 10kΩ_3.Pin_0, 10kΩ_4.Pin_1
  N15: R_GPIO2.pin23, GPIO3.pin4
  N16: R_GPIO2.pin24, GPIO3.pin3
  N17: R_GPIO2.pin25, GPIO3.pin2
  N18: R_GPIO2.pin26, GPIO3.pin1
  N19: R_GPIO2.pin29, SPI2.pin3
  N20: R_GPIO2.pin30, SPI2.pin2
  N21: R_GPIO2.pin31, SPI2.pin1
  N22: R_GPIO2.pin32, SPI3.pin2
  N23: R_GPIO2.pin33, GPIO2.pin4
  N24: R_GPIO2.pin34, GPIO2.pin3
  N25: R_GPIO2.pin35, GPIO2.pin2
  N26: R_GPIO2.pin37, GPIO2.pin1
  N27: R_GPIO2.pin38, IC2.pin11, MCP23021.pin11, UART240.pin7, UART240.pin8, UART240.pin9, UART240.pin10, UART240.pin11, UART240.pin12, IC10.pin12, IC5.pin12, GPIO5.pin3, UART292.pin2, UART304.pin3
  N28: R_GPIO2.pin39, IC2.pin13, MCP23021.pin13, UART240.pin1, UART240.pin2, UART240.pin3, UART240.pin4, UART240.pin5, UART240.pin6, IC10.pin13, IC5.pin13, GPIO5.pin4, UART292.pin3, UART304.pin2
  N29: R_GPIO2.pin40, SPI4.pin2
  N30: J61.pin1, UART233.pin1, UART238.pin2, UART246.pin1, UART247.pin1, UART247.pin2, UART247.pin3, UART247.pin4, UART269.pin2, 560kΩ.Pin_0, S25.4, J190.pin3, 10uF_50V.+
  N31: J61.pin2, S25.2
  N32: UART227.pin2, UART228.pin1
  N33: UART227.pin3, UART228.pin2
  N34: UART227.pin4, UART228.pin3
  N35: UART227.pin5, UART228.pin4
  N36: UART227.pin6, UART228.pin5
  N37: UART227.pin7, UART228.pin6
  N38: UART227.pin8, UART228.pin7
  N39: UART227.pin9, UART228.pin8
  N40: UART234.pin1, UART237.pin1
  N41: UART242.pin1, UART246.pin2
  N42: UART243.pin1, J142.pin1, J142.pin2, UART277.pin1, UART277.pin2, UART277.pin3, UART277.pin4, UART277.pin5, UART277.pin6, UART277.pin7, UART277.pin8
  N43: U1.DIS, U1.THR, 100uF.+
  N44: U1.CV, 10nF_4.1
  N45: U1.OUT, 10nF.0
  N46: U1.TRIG, 10kΩ_2.Pin_0, 10nF_3.1
  N47: U1.TRIG2, 10nF.1, 10kΩ.Pin_0
  N48: U1.OUT2, 1N4007_2.cathode
  N49: U1.CV2, 10nF_2.0
  N50: U1.THR2, U1.DIS2, 560kΩ_2.Pin_1, 100nF_9.0
  N51: 220uF_16V.+, UART226.pin1, IC1.1_2EN, IC1.3_4EN, IC2.pin1, IC2.pin4, IC2.pin9, 10uF.+, UART275.pin1, UART275.pin2, UART275.pin3, UART275.pin4, UART275.pin5, UART275.pin6, UART275.pin7, UART275.pin8, UART276.pin1, UART276.pin2, UART276.pin3, UART276.pin4, UART276.pin5, UART276.pin6, UART276.pin7, UART276.pin8, J139.pin1, J139.pin2, J140.pin1, J140.pin2, MCP23021.pin1, 100nF_3.1, UART281.pin2, 100nF_4.1, 10uF_4.+, 100nF_5.1, 10uF_5.+, UART271.pin1, UART271.pin2, UART271.pin3, UART271.pin4, UART271.pin5, UART271.pin6, IC10.pin9, IC10.pin18, 100nF_6.1, 10uF_6.+, 100nF_7.1, IC5.pin9, IC5.pin15, IC5.pin18, GPIO5.pin1, UART300.pin1, UART292.pin1, 10uF_7.+, SPI3.pin1, SPI4.pin1, 10uF_9.+, J190.pin1, UART302.pin1, UART302.pin2, UART302.pin3, UART302.pin4, UART302.pin5, UART302.pin6, UART302.pin7, 100nF_8.1, UART303.pin2, UART304.pin1, 430Ω.Pin_0
  N52: 10nF_2.1, BC547B.C
  N53: BC547B.E, 10nF_3.0, 4k7Ω.Pin_0
  N54: BC547B.B, 270kΩ.Pin_0
  N55: 270kΩ.Pin_1, IC2.pin3, 47Ω.Pin_0
  N56: UART255.pin1, UART255.pin2, UART255.pin3, UART255.pin4, UART255.pin5, UART255.pin6, UART255.pin7, UART255.pin8, UART256.pin1, UART256.pin2, UART256.pin3, UART256.pin4, UART256.pin5, UART256.pin6, UART256.pin7, UART256.pin8
  N57: J133.pin1, J133.pin2, J134.pin1, J134.pin2
  N58: IC1.1A, IC2.pin5, UART305.pin2
  N59: IC1.1Y, FUSE_2.2
  GND1: IC1.GND1, IC1.GND2
  N60: IC1.2A, IC2.pin8, UART305.pin1
  N61: IC1.VCC2, UART269.pin1, 1uF.+
  N62: IC1.3A, IC2.pin2, UART305.pin3
  GND3: IC1.GND3, IC1.GND4, 100nF_2.0
  N63: IC1.4Y, FUSE.2
  N64: IC1.4A, IC2.pin17, UART305.pin4
  N65: IC2.pin6, UART268.pin2, LED_1.anode
  N66: IC2.pin7, 47Ω_2.Pin_1
  N67: IC2.pin14, UART267.pin2, LED_2.anode
  N68: IC2.pin15, UART266.pin2, LED_3.anode
  N69: IC2.pin16, UART265.pin2, LED_4.anode
  N70: IC2.pin18, UART264.pin2, LED_5.anode
  N71: IC2.pin19, UART263.pin2, LED_6.anode
  N72: IC2.pin20, 100nF_7.0
  N73: UART263.pin1, LED_6.cathode
  N74: UART264.pin1, LED_5.cathode
  N75: UART265.pin1, LED_4.cathode
  N76: UART266.pin1, LED_3.cathode
  N77: UART267.pin1, LED_2.cathode
  N78: UART268.pin1, LED_1.cathode
  N79: 10uF_3.-, 100nF_9.1
  N80: MCP23021.pin2, J147.pin3
  N81: MCP23021.pin3, J147.pin2
  N82: MCP23021.pin4, MCP23021.pin5, MCP23021.pin6
  N83: MCP23021.pin7, J147.pin1
  N84: MCP23021.pin8, J148.pin3
  N85: MCP23021.pin9, J148.pin2
  N86: MCP23021.pin10, J148.pin1
  N87: MCP23021.pin12, J149.pin1
  N88: MCP23021.pin14, J149.pin2
  N89: MCP23021.pin15, J149.pin3
  N90: MCP23021.pin16, J150.pin1
  N91: MCP23021.pin18, J150.pin2
  N92: MCP23021.pin19, J150.pin3
  N93: MCP23021.pin20, 100nF_3.0
  N94: J151.pin1, J151.pin2, J151.pin3, J151.pin4, J154.pin1, J154.pin2, J154.pin3
  N95: J152.pin1, J152.pin2, J152.pin3, J152.pin4, J156.pin1, J156.pin2, J156.pin3
  N96: J153.pin1, J153.pin2, J153.pin3
  N97: J155.pin1, J155.pin2, J155.pin3
  N98: J158.pin1, J158.pin2, J158.pin3, IC10.pin15, IC10.pin16, IC10.pin17, J157.pin1, J157.pin2, J157.pin3
  N99: UART278.pin1, BT_ON.cathode
  N100: UART278.pin2, BT_ON.anode
  N101: UART279.pin1, NET.cathode
  N102: UART279.pin2, NET.anode, 56Ω.Pin_0
  N103: UART281.pin1, POWER_IS_ON.cathode
  N104: POWER_IS_ON.anode, 430Ω.Pin_1
  N105: UART282.pin1, LOW_BAT.cathode
  N106: UART282.pin2, LOW_BAT.anode, 47Ω_2.Pin_0
  N107: UART283.pin1, POWERING_OFF.cathode
  N108: UART283.pin2, POWERING_OFF.anode, 47Ω.Pin_1
  N109: UART284.pin1, OK.cathode
  N110: UART284.pin2, OK.anode, 47Ω_3.Pin_1
  N111: UART285.pin1, ERROR.cathode
  N112: UART285.pin2, ERROR.anode, 47Ω_4.Pin_1
  N113: DIP_SWITCH.pin1, UART286.pin6
  N114: DIP_SWITCH.pin2, UART286.pin5
  N115: DIP_SWITCH.pin3, UART286.pin4
  N116: DIP_SWITCH.pin4, UART286.pin3
  N117: DIP_SWITCH.pin5, UART286.pin2
  N118: DIP_SWITCH.pin6, UART286.pin1
  N119: DIP_SWITCH.pin7, UART287.pin1, IC5.pin6
  N120: DIP_SWITCH.pin8, UART287.pin2, IC5.pin5
  N121: DIP_SWITCH.pin9, UART287.pin3, IC5.pin4
  N122: DIP_SWITCH.pin10, UART287.pin4, IC5.pin3
  N123: DIP_SWITCH.pin11, UART287.pin5, IC5.pin2
  N124: DIP_SWITCH.pin12, UART287.pin6, IC5.pin1
  N125: S17.1, J167.pin2
  N126: S17.3, J167.pin1, IC5.pin7
  N127: S18.1, J165.pin2
  N128: S18.3, J165.pin1, IC5.pin8
  N129: S19.leg0, J168.pin3, IC5.pin26
  N130: S19.leg1, S20.leg1, S21.leg1, S22.leg1, S23.leg1, S24.leg1, J170.pin1, J170.pin2, J170.pin3, J185.pin1, J185.pin2, J185.pin3
  N131: S20.leg0, J168.pin2, IC5.pin25
  N132: S21.leg0, J168.pin1, IC5.pin24
  N133: S22.leg0, J169.pin3, IC5.pin23
  N134: S23.leg0, J169.pin2, IC5.pin22
  N135: S24.leg0, J169.pin1, IC5.pin21
  N136: 100nF_4.0, 10uF_4.-, IC5.pin10
  N137: 100nF_5.0, UART291.pin1
  N138: UART293.pin1, UART291.pin2
  N139: UART293.pin2, UART291.pin3
  N140: UART293.pin3, UART291.pin4
  N141: UART293.pin4, UART291.pin5
  N142: 560kΩ.Pin_1, 75kΩ.Pin_1
  N143: ULN2803A1.pin1, IC10.pin28
  N144: ULN2803A1.pin2, IC10.pin27
  N145: ULN2803A1.pin3, IC10.pin26
  N146: ULN2803A1.pin4, IC10.pin25
  N147: ULN2803A1.pin5, IC10.pin24
  N148: ULN2803A1.pin6, IC10.pin23
  N149: ULN2803A1.pin7, IC10.pin22
  N150: ULN2803A1.pin8, IC10.pin21
  N151: ULN2803A1.pin10, UART297.pin9
  N152: ULN2803A1.pin11, UART297.pin8
  N153: ULN2803A1.pin12, UART297.pin7
  N154: ULN2803A1.pin13, UART297.pin6
  N155: ULN2803A1.pin14, UART297.pin5
  N156: ULN2803A1.pin15, UART297.pin4
  N157: ULN2803A1.pin16, UART297.pin3
  N158: ULN2803A1.pin17, UART297.pin2
  N159: ULN2803A1.pin18, UART297.pin1
  N160: UART272.pin1, UART272.pin2, UART272.pin3, UART272.pin4, UART272.pin5, UART272.pin6
  N161: IC10.pin1, J189.pin8
  N162: IC10.pin2, J189.pin7
  N163: IC10.pin3, J189.pin6
  N164: IC10.pin4, J189.pin5
  N165: IC10.pin5, J189.pin4
  N166: IC10.pin6, J189.pin3
  N167: IC10.pin7, J189.pin2
  N168: IC10.pin8, J189.pin1
  N169: IC10.pin10, 100nF_6.0, 10uF_6.-
  N170: IC10.pin20, 10kΩ_4.Pin_0
  N171: 10kΩ_3.Pin_1, IC5.pin20
  N172: 47Ω_3.Pin_0, IC5.pin27
  N173: 47Ω_4.Pin_0, IC5.pin28
  N174: IC5.pin16, IC5.pin17
  N175: 1N4007.A, 1N4007_2.anode
  N176: UART301.pin1, UART301.pin2, UART301.pin3, UART301.pin4, UART301.pin5, UART301.pin6, UART301.pin7

notes:
  4_23
  5_24
  6_25
  1_14
  2_15
  PCM
  8_7
  CE0
  18_9
  13_4
  10-16
  9-12
  14_17
  11_20
  15_27
  12_21
  GPIO
  17_10
  16_22
  20_5
  21_6
  22_13
  23_19
  19_11
  BYPASS_5V_REG
  MAIN_POWER_OUT
  MAIN_POWER_IN
  V_MAIN
  V_IN
  SCREW_TERMINAL
  MAIN_RELAY
  SRD-05VDC-SL-C
  5V
  OFF
  GND
  1N4007
  Main Power OUT
  V_OUT
  Screw terminal
  ON
  POWER
  <GND
  LEV_CON
  ADAFRUIT: TXB0108
  3V3
  -------GPIO_5V-------
  3_18
  7_8
  -- GPIO_3V3 --
  GPIO_3V3>
  MP1584EN_5V
  <5V_REG
  BYPASS_5V_REG>
  POWER_IS_ON
  OFF_SIG
  SIG
  ---   -I2C------
  SDA
  SCL
  POWER_ON
  MP1584EN
  V_ADJ
  <V_ADJ_ON
  ------TLC556CN------
  DSCH
  -
  220µF
  OE
  VCCA
  VCCB
  220µF_35V
  CONT
  VDD
  RESE
  THRE
  OUT
  TRIG
  100nF
  10nF
  10kΩ
  BC547B
  4k7Ω
  270kΩ
  DELAY_POW_OFF
  500kΩ
  TRIM
  +
  10uF
  POWERING_OFF
  ----5V----
  ----3V3----
  ----GND----
  MOTOR_2
  MOTOR_1
  SN754410NE
  M1
  V_M
  -GND-
  M2
  FOR
  REV
  P016-I2C I2C=36
  PWM1
  PWM2
  PWM3
  PWM4
  IO1
  IO2
  IO3
  IO4
  IO6
  IO8
  IO5
  IO7
  N/C
  GND SIG
  LED_6
  LED_1
  GND 3V3
  LED_5
  LED_4
  LED_3
  LED_2
  V
  MAIN
  V_M: DC voltage
  1uF
  LOW_BAT
  VREF
  AN6
  AN4
  D1
  AN7
  P012_I2C
  AN2
  AN8
  AN1
  D3
  D2
  AN5
  AN3
  --
  SRV
  S3
  S5
  S6
  S7
  S8
  S9
  S10
  S11
  12
  10
  3
  -SRV-
  -SIG-
  11
  9
  8
  7
  2
  6
  4
  5
  1
  S0
  S1
  AD2
  AD1
  AD0
  S2
  S4
  I2C=28
  -SERVO-
  SUM
  BUTTON
  BT_ON
  NET
  <10uF
  47Ω
  OK
  ERROR
  B>
  MCP23017
  0
  3>5V
  A0 A1 A2
  <A
  B
  A
  POWER_OFF
  INFO
  MCP4728 I2C=61
  Vo3
  MCP4728
  Vo0
  Vo2
  Vo1
  DAC
  --SIG--
  ----SWITCH----
  6_PIN_DIP_SWITCH
  560kΩ
  75kΩ
  -------ULN2803A-------
  com
  COM
  OU7
  OU3
  OU1
  OU4
  OU6
  OU8
  OU5
  OU2
  IN8
  IN7
  IN6
  IN5
  IN4
  IN3
  IN2
  IN1
  MOSI
  MISO
  CLK
  XGPIO
  OLED_LCD
  MCP23017 I2C=20
  MCP23017 I2C=21
  I2C=3C
  TRIGGER>
  I2C=34
  56Ω
  BLUE
  SCREW
  TERMINAL
  YELLOW
  RED
  ORANGE
  BLACK
  WHITE
  GREEN
  \__/
  I2C=61
  VOLT
  GPIO_3V3
  ACC_GYRO
  STEELSQUID.ORG
  STEELSQUID_PIIO
  2015-06-02
  1V0
  PCB-TOP
  PCB-BOTTOM
  C
  E
  FEMALE
  PINS
  FEM PINS
  -----
  CE1
  TXD
  RXD
  HiV
  LoV
  -OR-
  EZSCB: LS1
  TXB0108 >
  LS1 >
  _
  0>3V3
  V_SERVO>
  ----
  <    >
  PI_3V3
  PI_3V3_REG
  >
  <ADC_0>3V3
  16V
  35V
  220µF_16V
  EXTERNAL
  3V3_REG
  REG
  FROM
  FEMALE_PINS
  CONNECT_PI
  <I2C=69
  D24V10F3
  MAIN_POWER_IN=8-26V
  <
  MAIN_POWER_IN=5V
  10uF_50V
  PTC_FUSE
  10nF>
  100uF
  SERVO12C(HT)
  <GREETECH_MPU-6050
  430Ω
  <560kΩ
  ---PWM---
