# Fritzing sketch steelsquid_PI_IO (saved by Fritzing 0.9.1b)
circuit board: 12cm x 10cm
breadboards: 1

parts:
  UART77 = male pin header, 8 pins [form="♂ (male)"]
  UART78 = male pin header, 10 pins [form="♂ (male)"]
  UART79 = male pin header, 9 pins [form="♂ (male)"]
  J6 = male pin header, 4 pins [form="♂ (male)"]
  J1 = double row female pin header, 40 pins [form="♀ (female)"]
  J7 = male pin header, 5 pins [form="♂ (male)"]
  J8 = male pin header, 3 pins [form="♂ (male)"]
  J9 = male pin header, 4 pins [form="♂ (male)"]
  J5 = male pin header, 2 pins [form="♂ (male)"]
  J4 = male pin header, 3 pins [form="♂ (male)"]
  J3 = male pin header, 1 pin [form="♂ (male)"]
  J2 = male pin header, 2 pins [form="♂ (male)"]
  J16 = screw terminal, 2 pins
  UART81 = male pin header, 3 pins [form="♂ (male)"]
  J22 = screw terminal, 2 pins
  J23 = screw terminal, 2 pins
  J24 = screw terminal, 2 pins
  UART82 = double row male pin header, 16 pins [form="♂ (male)"]
  MCP23018 = IC, DIP package, 28 pins [chip_label=IC]
  TLC555CP = General purpose bipolar Timer [package=dil-08]
  BC547B = TRANSISTOR_NPN [package=to-92-ammo]
  10KΩ = Resistor [tolerance=±5% resistance=220 package=THT]
  BC547B_2 = TRANSISTOR_NPN [package=to-92-ammo]
  1000μF = Electrolytic Capacitor [capacitance=1000μF voltage=20V package="200 mil [THT, electrolytic]"]
  2_2K = Resistor [tolerance=±5% resistance=220 package=THT]
  P_ON = Momentary Switch [package=ksa_sealed_tac_switch]
  J25 = male pin header, 1 pin [form="♂ (male)"]
  J26 = male pin header, 1 pin [form="♂ (male)"]
  J29 = screw terminal, 2 pins
  J31 = screw terminal, 2 pins
  UART84 = male pin header, 4 pins [form="♂ (male)"]
  UART85 = male pin header, 5 pins [form="♂ (male)"]
  UART86 = male pin header, 5 pins [form="♂ (male)"]
  UART88 = male pin header, 6 pins [form="♂ (male)"]
  UART89 = male pin header, 4 pins [form="♂ (male)"]
  UART90 = male pin header, 4 pins [form="♂ (male)"]
  DIP = IC, DIP package, 8 pins [chip_label=DIP]
  ERROR = LED - 3mm [color="Red (660nm)" package="3 mm [THT]"]
  OK = LED - 3mm [color="Green (570nm)" package="3 mm [THT]"]
  PUSH_1 = Momentary Switch [package=ksa_sealed_tac_switch]
  PUSH_2 = Momentary Switch [package=ksa_sealed_tac_switch]
  PUSH_3 = Momentary Switch [package=ksa_sealed_tac_switch]
  J54 = male pin header, 1 pin [form="♂ (male)"]  # not connected
  INFO = Momentary Switch [package=ksa_sealed_tac_switch]
  UART95 = male pin header, 8 pins [form="♂ (male)"]
  ULN2803A = IC, DIP package, 18 pins [chip_label=IC]
  UART97 = male pin header, 4 pins [form="♂ (male)"]
  UART99 = double row male pin header, 12 pins [form="♂ (male)"]
  J59 = male pin header, 2 pins [form="♂ (male)"]
  J60 = male pin header, 2 pins [form="♂ (male)"]
  J61 = male pin header, 2 pins [form="♂ (male)"]
  J62 = male pin header, 2 pins [form="♂ (male)"]
  J63 = male pin header, 4 pins [form="♂ (male)"]
  J64 = male pin header, 4 pins [form="♂ (male)"]
  J65 = male pin header, 4 pins [form="♂ (male)"]
  100K = Resistor [tolerance=±5% resistance=220 package=THT]
  560K = Resistor [tolerance=±5% resistance=220 package=THT]
  J66 = double row male pin header, 4 pins [form="♂ (male)"]
  UART101 = male pin header, 4 pins [form="♂ (male)"]
  UART100 = male pin header, 6 pins [form="♂ (male)"]
  MCP23019 = IC, DIP package, 20 pins [chip_label=IC]
  J70 = double row male pin header, 14 pins [form="♂ (male)"]
  J75 = male pin header, 2 pins [form="♂ (male)"]
  INFO2 = Momentary Switch [package=ksa_sealed_tac_switch]
  UART104 = male pin header, 4 pins [form="♂ (male)"]
  UART106 = male pin header, 3 pins [form="♂ (male)"]
  UART107 = male pin header, 2 pins [form="♂ (male)"]
  J80 = male pin header, 1 pin [form="♂ (male)"]
  ERROR1 = LED - 3mm [color="Blue (470nm)" package="3 mm [THT]"]
  10nF = Ceramic Capacitor [capacitance=10nF package="100 mil [THT, multilayer]"]
  1K = Resistor [tolerance=±5% resistance=1k package=THT]
  ERROR2 = LED - 3mm [color="Yellow (592nm)" package="3 mm [THT]"]
  UART87 = male pin header, 2 pins [form="♂ (male)"]
  UART98 = male pin header, 2 pins [form="♂ (male)"]
  UART83 = double row male pin header, 16 pins [form="♂ (male)"]
  10nF_2 = Ceramic Capacitor [capacitance=10nF package="100 mil [THT, multilayer]"]
  UART103 = male pin header, 3 pins [form="♂ (male)"]
  UART108 = male pin header, 3 pins [form="♂ (male)"]
  UART102 = male pin header, 3 pins [form="♂ (male)"]
  J81 = double row male pin header, 2 pins [form="♂ (male)"]
  J82 = double row male pin header, 2 pins [form="♂ (male)"]
  J83 = double row male pin header, 2 pins [form="♂ (male)"]
  UART109 = double row male pin header, 4 pins [form="♂ (male)"]
  UART110 = double row male pin header, 8 pins [form="♂ (male)"]
  UART115 = male pin header, 1 pin [form="♂ (male)"]
  UART113 = male pin header, 1 pin [form="♂ (male)"]
  UART114 = male pin header, 1 pin [form="♂ (male)"]
  UART116 = male pin header, 1 pin [form="♂ (male)"]
  UART117 = male pin header, 1 pin [form="♂ (male)"]
  UART118 = male pin header, 1 pin [form="♂ (male)"]
  J79 = male pin header, 3 pins [form="♂ (male)"]
  J78 = male pin header, 4 pins [form="♂ (male)"]
  J77 = male pin header, 3 pins [form="♂ (male)"]
  J94 = male pin header, 3 pins [form="♂ (male)"]
  J95 = male pin header, 3 pins [form="♂ (male)"]
  J96 = male pin header, 3 pins [form="♂ (male)"]
  J97 = male pin header, 1 pin [form="♂ (male)"]
  J98 = male pin header, 3 pins [form="♂ (male)"]
  J99 = male pin header, 3 pins [form="♂ (male)"]
  J100 = male pin header, 4 pins [form="♂ (male)"]
  J101 = male pin header, 3 pins [form="♂ (male)"]
  J102 = male pin header, 3 pins [form="♂ (male)"]
  J103 = male pin header, 3 pins [form="♂ (male)"]
  UART80 = double row male pin header, 8 pins [form="♂ (male)"]
  J73 = male pin header, 2 pins [form="♂ (male)"]
  UART119 = male pin header, 1 pin [form="♂ (male)"]
  UART111 = male pin header, 6 pins [form="♂ (male)"]
  UART112 = male pin header, 6 pins [form="♂ (male)"]
  UART120 = male pin header, 5 pins [form="♂ (male)"]
  UART121 = male pin header, 5 pins [form="♂ (male)"]
  UART122 = male pin header, 11 pins [form="♂ (male)"]
  UART123 = male pin header, 11 pins [form="♂ (male)"]
  ULN2803A_2 = IC, DIP package, 18 pins [chip_label=IC]
  UART124 = male pin header, 8 pins [form="♂ (male)"]
  J104 = male pin header, 2 pins [form="♂ (male)"]  # not connected
  J105 = male pin header, 1 pin [form="♂ (male)"]  # not connected

nets:
  N1: UART77.pin1, UART78.pin2
  N2: UART77.pin2, UART78.pin3
  N3: UART77.pin3, UART78.pin4
  N4: UART77.pin4, UART78.pin5
  N5: UART77.pin5, UART78.pin6
  N6: UART77.pin6, UART78.pin7
  N7: UART77.pin7, UART78.pin8
  N8: UART77.pin8, UART78.pin9
  N9: UART78.pin1, J1.pin39, J1.pin40, UART81.pin2, TLC555CP._RES, TLC555CP.VCC+, 10KΩ.Pin_1, 2_2K.Pin_1, J29.pin1, J29.pin2, J65.pin1, J65.pin2, J65.pin3, J65.pin4, UART100.pin2, UART100.pin6, J70.pin1, J70.pin2, J70.pin3, J70.pin4, J70.pin5, J70.pin6, J70.pin7, J70.pin8, J70.pin9, J70.pin10, J70.pin11, J70.pin12, J70.pin13, J70.pin14, J80.pin1, UART103.pin1, UART108.pin1, UART102.pin3, J82.pin1, J82.pin2, UART109.pin1, UART109.pin2, UART109.pin3, UART109.pin4, UART113.pin1, J97.pin1, UART119.pin1
  N10: UART78.pin10, J1.pin26, J1.pin38, UART81.pin1, J22.pin1, J22.pin2, J23.pin1, J24.pin1, UART82.pin1, UART82.pin2, UART82.pin3, UART82.pin4, UART82.pin5, UART82.pin6, UART82.pin7, UART82.pin8, UART82.pin9, UART82.pin10, UART82.pin11, UART82.pin12, UART82.pin13, UART82.pin14, UART82.pin15, UART82.pin16, MCP23018.pin10, MCP23018.pin15, MCP23018.pin16, MCP23018.pin17, TLC555CP.GND, BC547B.C, BC547B_2.C, 1000μF.-, UART85.pin1, UART88.pin2, UART88.pin5, ERROR.cathode, OK.cathode, ULN2803A.pin9, 100K.Pin_0, UART100.pin5, MCP23019.pin4, MCP23019.pin5, MCP23019.pin6, MCP23019.pin20, UART104.pin2, UART107.pin2, 10nF.0, ERROR2.cathode, 10nF_2.1, UART103.pin3, UART108.pin3, UART102.pin1, J81.pin1, J81.pin2, UART110.pin1, UART110.pin2, UART110.pin3, UART110.pin4, UART110.pin5, UART110.pin6, UART110.pin7, UART110.pin8, UART114.pin1, UART116.pin1, J101.pin1, J101.pin2, J101.pin3, J103.pin1, J103.pin2, J103.pin3, UART112.pin6
  N11: UART79.pin1, J1.pin9, MCP23018.pin9, MCP23018.pin18, DIP.pin1, DIP.pin2, DIP.pin3, DIP.pin4, PUSH_1.3, PUSH_2.3, PUSH_3.1, INFO.4, J60.pin2, J61.pin2, J62.pin1, J63.pin1, J63.pin2, J63.pin3, J63.pin4, MCP23019.pin1, INFO2.4, UART104.pin1, UART106.pin3, UART107.pin1, ERROR1.anode, J83.pin1, J83.pin2
  N12: UART79.pin2, J6.pin1, J1.pin25
  N13: UART79.pin3, J6.pin2, J1.pin23
  N14: UART79.pin4, J6.pin3, J1.pin22
  N15: UART79.pin5, J6.pin4, J1.pin21
  N16: UART79.pin6, J1.pin19, J7.pin5
  N17: UART79.pin7, J1.pin18, J7.pin4
  N18: UART79.pin8, J1.pin17, J7.pin3
  N19: UART79.pin9, J1.pin16, J7.pin2
  N20: J1.pin1, J31.pin1, J31.pin2, UART87.pin2, UART98.pin2, UART83.pin1, UART83.pin2, UART83.pin3, UART83.pin4, UART83.pin5, UART83.pin6, UART83.pin7, UART83.pin8, UART83.pin9, UART83.pin10, UART83.pin11, UART83.pin12, UART83.pin13, UART83.pin14, UART83.pin15, UART83.pin16
  N21: J1.pin2, MCP23018.pin13, UART86.pin3, UART88.pin3, UART99.pin1, UART99.pin2, UART99.pin3, UART99.pin4, UART99.pin5, UART99.pin6
  N22: J1.pin3, MCP23018.pin12, UART86.pin2, UART88.pin4, UART99.pin7, UART99.pin8, UART99.pin9, UART99.pin10, UART99.pin11, UART99.pin12
  N23: J1.pin4, J9.pin1
  N24: J1.pin6, J9.pin2
  N25: J1.pin7, J9.pin3
  N26: J1.pin8, J9.pin4
  N27: J1.pin10, J8.pin1
  N28: J1.pin11, J8.pin2
  N29: J1.pin12, J8.pin3
  N30: J1.pin13, ERROR1.cathode
  N31: J1.pin15, J7.pin1
  N32: J1.pin28, J5.pin2
  N33: J1.pin29, J5.pin1
  N34: J1.pin30, J4.pin3
  N35: J1.pin32, J4.pin2
  N36: J1.pin33, J4.pin1
  N37: J1.pin35, J3.pin1
  N38: J1.pin36, J2.pin2
  N39: J1.pin37, J2.pin1
  N40: J16.pin1, J16.pin2, UART118.pin1, UART80.pin1, UART80.pin2, UART80.pin3, UART80.pin4, UART80.pin5, UART80.pin6, UART80.pin7, UART80.pin8
  N41: UART81.pin3, BC547B_2.E, 2_2K.Pin_0
  N42: J23.pin2, J24.pin2, P_ON.2, 560K.Pin_1, UART117.pin1, J73.pin2
  N43: MCP23018.pin1, ULN2803A.pin4
  N44: MCP23018.pin2, ULN2803A.pin3
  N45: MCP23018.pin3, ULN2803A.pin2
  N46: MCP23018.pin4, ULN2803A.pin1
  N47: MCP23018.pin5, BC547B.B
  N48: MCP23018.pin6, PUSH_1.2
  N49: MCP23018.pin7, PUSH_3.4
  N50: MCP23018.pin8, PUSH_2.2
  N51: MCP23018.pin21, DIP.pin7, J64.pin3
  N52: MCP23018.pin22, DIP.pin6, J64.pin2
  N53: MCP23018.pin23, DIP.pin5, J64.pin1
  N54: MCP23018.pin24, DIP.pin8, J64.pin4
  N55: MCP23018.pin25, J75.pin2, INFO2.1
  N56: MCP23018.pin26, ERROR.anode
  N57: MCP23018.pin27, OK.anode
  N58: MCP23018.pin28, INFO.1, J59.pin2
  N59: TLC555CP.TRI, BC547B.E, 10KΩ.Pin_0, 10nF_2.0
  N60: TLC555CP.OUT, 1K.Pin_1
  N61: TLC555CP.CON, 10nF.1
  N62: TLC555CP.TRE, TLC555CP.DIS
  N63: BC547B_2.B, 1000μF.+
  N64: P_ON.1, J25.pin1
  N65: P_ON.3, J26.pin1
  N66: UART84.pin1, UART85.pin2
  N67: UART84.pin2, UART85.pin3
  N68: UART84.pin3, UART85.pin4
  N69: UART84.pin4, UART85.pin5
  N70: UART86.pin1, UART87.pin1
  N71: UART88.pin6, UART98.pin1
  N72: UART89.pin1, UART90.pin1
  N73: UART89.pin2, UART90.pin2
  N74: UART89.pin3, UART90.pin3
  N75: UART89.pin4, UART90.pin4
  N76: PUSH_1.1, J60.pin1
  N77: PUSH_2.1, J61.pin1
  N78: PUSH_3.3, J62.pin2
  N79: INFO.3, J59.pin1
  N80: UART95.pin1, ULN2803A.pin18
  N81: UART95.pin2, ULN2803A.pin17
  N82: UART95.pin3, ULN2803A.pin16
  N83: UART95.pin4, ULN2803A.pin15
  N84: UART95.pin5, ULN2803A.pin14
  N85: UART95.pin6, ULN2803A.pin13
  N86: UART95.pin7, ULN2803A.pin12
  N87: UART95.pin8, ULN2803A.pin11
  N88: ULN2803A.pin5, UART97.pin1
  N89: ULN2803A.pin6, UART97.pin2
  N90: ULN2803A.pin7, UART97.pin3
  N91: ULN2803A.pin8, UART97.pin4
  N92: 100K.Pin_1, 560K.Pin_0, UART101.pin3
  N93: J66.pin1, J66.pin4, MCP23019.pin11, UART104.pin3, UART106.pin1
  N94: J66.pin2, J66.pin3, MCP23019.pin13, UART104.pin4, UART106.pin2
  N95: UART101.pin1, UART103.pin2
  N96: UART101.pin2, UART108.pin2
  N97: UART101.pin4, UART102.pin2
  N98: MCP23019.pin2, J99.pin3
  N99: MCP23019.pin3, J99.pin2
  N100: MCP23019.pin7, J99.pin1
  N101: MCP23019.pin8, J98.pin3
  N102: MCP23019.pin9, J98.pin2
  N103: MCP23019.pin10, J98.pin1
  N104: MCP23019.pin12, J96.pin1
  N105: MCP23019.pin14, J96.pin2
  N106: MCP23019.pin15, J96.pin3
  N107: MCP23019.pin16, J79.pin1
  N108: MCP23019.pin18, J79.pin2
  N109: MCP23019.pin19, J79.pin3
  N110: J75.pin1, INFO2.3
  N111: 1K.Pin_0, ERROR2.anode
  N112: UART115.pin1, J73.pin1
  N113: J78.pin1, J78.pin2, J78.pin3, J78.pin4, J95.pin1, J95.pin2, J95.pin3
  N114: J77.pin1, J77.pin2, J77.pin3, J94.pin1, J94.pin2, J94.pin3
  N115: J100.pin1, J100.pin2, J100.pin3, J100.pin4, J102.pin1, J102.pin2, J102.pin3
  N116: UART111.pin1, UART121.pin1
  N117: UART111.pin2, UART121.pin2
  N118: UART111.pin3, UART121.pin3
  N119: UART111.pin4, UART121.pin4
  N120: UART111.pin5, UART121.pin5
  N121: UART112.pin1, UART120.pin1
  N122: UART112.pin2, UART120.pin2
  N123: UART112.pin3, UART120.pin3
  N124: UART112.pin4, UART120.pin4
  N125: UART112.pin5, UART120.pin5
  N126: UART122.pin1, ULN2803A_2.pin9
  N127: UART122.pin7, ULN2803A_2.pin8
  N128: UART122.pin8, ULN2803A_2.pin7
  N129: UART122.pin9, ULN2803A_2.pin6
  N130: UART122.pin10, ULN2803A_2.pin5
  N131: UART122.pin11, ULN2803A_2.pin4
  N132: UART123.pin1, UART123.pin11
  N133: UART123.pin8, ULN2803A_2.pin3
  N134: UART123.pin9, ULN2803A_2.pin2
  N135: UART123.pin10, ULN2803A_2.pin1
  N136: ULN2803A_2.pin11, UART124.pin8
  N137: ULN2803A_2.pin12, UART124.pin7
  N138: ULN2803A_2.pin13, UART124.pin6
  N139: ULN2803A_2.pin14, UART124.pin5
  N140: ULN2803A_2.pin15, UART124.pin4
  N141: ULN2803A_2.pin16, UART124.pin3
  N142: ULN2803A_2.pin17, UART124.pin2
  N143: ULN2803A_2.pin18, UART124.pin1

notes:
  GND
  i2C
  SCL
  SDA
  17
  XGPIO5VA20
  I2C
  ADJ
  UART_4
  DAC_61_5V
  Vo3
  3
  4
  Vo2
  Vo1
  Vo0
  MCP4728
  +5V
  1
  2
  UART
  RXD
  TXD
  Ø3.5mm
  +3V3
  1-14-TXD
  2-15-RXD
  3-18-PCM
  4-23
  5-24
  6-25
  7-08-CE0
  8-07-CE1
  11-20
  12-21
  13-04
  20-05
  21-06
  22-13
  23-19
  24-26
  3V3 side
  5V side
  Adafruit 8C lev con
  9-12
  10-16
  +V_IN
  Screw terminal
  Main Power
  3V3<->5V
  GPIO_3V3
  +V
  on relay
  GPIO_23_5V
  0
  5
  6
  7
  3>5V
  A0 A1 A2
  -
  TR
  OU
  RE
  +
  DI
  TH
  CV
  500KΩ
  <Min
  <Max
  <>
  Adj Vol Reg (5V)
  GPIO_5V
  DAC
  ADDR
  ADC
  A3
  ADS1015
  A2
  A1
  A0
  8
  GPIO_22_XV
  C
  B
  D
  A
  SIGNAL
  POWER
  Max 50V in
  13
  04
  >
  14-17
  15-27
  16-22
  3V3
  19-11
  17-10
  18-09
  I2C SCL
  I2C SDA
  MOSI
  MISO-
  CLK-
  4PIN DIP
  SWITCH
  Ø3mm
  DAC&ADC
  Con 2.7 to 5.5 V to
  3.3>5.5V
  5V
  Push
  Input
  With LCD
  SUM
  < On PCB bottom
  INFO
  Long jumper
  PCB bot
  MAX 28V IN
  TRIM
  3V3>5V5
  AD
  Cop-Side
  Off
  Long jump bottom
  Long jump
  MCP9700T
  VDD
  VOUT
  TRIM_2
  Show IP
  (IP...)
  IP...
  Show
  POWER_ON
  OFF
  SIG
  +SRV
  0.96'' 128x64 OLED I2C
  GDN
  CS_03
  CS_04
  BJ_03
  BJ_05
  CS_01
  CS_02
  CS
  SparkFun
  SERVO12C(HT)
  MPU-6050
  BJ
  SERVO
  on LCD
  IN
  TRIM_1
  ON
  GND->
  9-
  10-
  LV
  HV
  LV: 2.8-HV
  Adaf. I2C lev con
  +OUT
  (5V) CS
  Vol Reg LM2596 (5V) Cip-Side
  Vol Reg (5V) CS
  +IN
  S0
  S1
  AD2
  AD1
  AD0
  S2
  S4
  S3
  S5
  S6
  S7
  S8
  S9
  S10
  S11
  12
  10
  11
  9
  V_ADJ
  V-Reg (5V) CS
  Delay-P-off
  Bypass
  Use-5V-Reg
  Vol-Reg
  ><
  min/2V8><10V/max
  <A1>
  <A2>
  V
  I2C/SPI
  IO3
  RX
  TX
  IO4
  IO5
  IO0
  IO1
  IO2
  VIN
  IO6
  IO7
  IO V1.0
  STEELSQUID
  CS = Copper Side (Bottom)
  16
